// Logisim project logisim-trinary-simulator.circ as structural Verilog: 44 circuits, main circuit Introduction and how trinary is modeled
module Introduction_and_how_trinary_is_modeled (
  input  [1:0] in_1,
  output out_2,
  output out_3,
  output out_4
);

  wire decoder_1_out0, decoder_1_out3, tri_led_driver_1_out_2, tri_led_driver_1_out_3, tri_led_driver_1_out_4;

  LED led_1 (.in(tri_led_driver_1_out_2));
  LED led_2 (.in(tri_led_driver_1_out_4));
  LED led_3 (.in(tri_led_driver_1_out_3));
  tri_led_driver tri_led_driver_1 (
    .in_1(in_1), .out_2(tri_led_driver_1_out_2), .out_3(tri_led_driver_1_out_3),
    .out_4(tri_led_driver_1_out_4));
  Decoder #(.select(2)) decoder_1 (
    .out0(decoder_1_out0), .out1(out_2), .out2(out_4), .out3(decoder_1_out3), .sel(in_1));
  or or_1 (out_3, decoder_1_out0, decoder_1_out3);

  // Notes on the sheet:
  //   This is *NOT* a valid (simulated) trinary circut.
  //   Its outputs are not (simulated) tri-level.
  //   It is usefull for building (simulations of) trinary circuits
  //   Although the *wires* are simulations, the
  //   gates are 'real' trinary gates.  If we could replace the
  //   split/joins with weird D/A circuits, it would be all real.
  //   Look at "TNAND fast" to see how the gates should be implemented in real hardware.
  //   This is all copyrighted, and licensed to you if you desire, under GPL 3 or later.
  //   Simple system for simulating trinary logic circuits.
  //   The usual sort of implementation is used here,
  //   we simulate a single wire with 3 level signals
  //    with a pair of wires carying two level signals.
  //   The high bit (Logisim is little endian, it is numbered 1) represents -1 often notated j
  //   The value 11 is considered non-standard, many circuits will treat it as 00 though.
  //   00 is used to represent 0 often notated o
  //   The low bit (numbered 0) represents +1 always notated 1
  //   Representation of +1 is on the pair of wires
  //   +1 asserted high
  //   0 asserted high
  //   -1 asserted high
endmodule

module Sampler__copy_LEDs_from_here (
  input  in_1
);

  wire _0_out, _1_out, _2_out, _3_out, _4_out, A_out, B_out, C_out, D_out, n2t_to_7seg_driver_1_out_2,
       n2t_to_7seg_driver_1_out_3, n2t_to_7seg_driver_1_out_4, n2t_to_7seg_driver_1_out_5,
       n2t_to_7seg_driver_1_out_6, n2t_to_7seg_driver_1_out_7, n2t_to_7seg_driver_1_out_8,
       n2t_to_7seg_driver_1_out_9, n2t_to_7seg_driver_2_out_2, n2t_to_7seg_driver_2_out_3,
       n2t_to_7seg_driver_2_out_4, n2t_to_7seg_driver_2_out_5, n2t_to_7seg_driver_2_out_6,
       n2t_to_7seg_driver_2_out_7, n2t_to_7seg_driver_2_out_8, n2t_to_7seg_driver_2_out_9,
       n2t_to_7seg_driver_3_out_2, n2t_to_7seg_driver_3_out_3, n2t_to_7seg_driver_3_out_4,
       n2t_to_7seg_driver_3_out_5, n2t_to_7seg_driver_3_out_6, n2t_to_7seg_driver_3_out_7,
       n2t_to_7seg_driver_3_out_8, n2t_to_7seg_driver_3_out_9, n2t_to_7seg_driver_4_out_2,
       n2t_to_7seg_driver_4_out_3, n2t_to_7seg_driver_4_out_4, n2t_to_7seg_driver_4_out_5,
       n2t_to_7seg_driver_4_out_6, n2t_to_7seg_driver_4_out_7, n2t_to_7seg_driver_4_out_8,
       n2t_to_7seg_driver_4_out_9, n2t_to_7seg_driver_5_out_2, n2t_to_7seg_driver_5_out_3,
       n2t_to_7seg_driver_5_out_4, n2t_to_7seg_driver_5_out_5, n2t_to_7seg_driver_5_out_6,
       n2t_to_7seg_driver_5_out_7, n2t_to_7seg_driver_5_out_8, n2t_to_7seg_driver_5_out_9,
       n2t_to_7seg_driver_6_out_2, n2t_to_7seg_driver_6_out_3, n2t_to_7seg_driver_6_out_4,
       n2t_to_7seg_driver_6_out_5, n2t_to_7seg_driver_6_out_6, n2t_to_7seg_driver_6_out_7,
       n2t_to_7seg_driver_6_out_8, n2t_to_7seg_driver_6_out_9, tri_led_driver_1_out_2,
       tri_led_driver_1_out_3, tri_led_driver_1_out_4, tri_led_driver_2_out_2, tri_led_driver_2_out_3,
       tri_led_driver_2_out_4, tri_led_driver_3_out_2, tri_led_driver_3_out_3, tri_led_driver_3_out_4,
       tri_led_driver_4_out_2, tri_led_driver_4_out_3, tri_led_driver_4_out_4, tri_led_driver_5_out_2,
       tri_led_driver_5_out_3, tri_led_driver_5_out_4, tri_led_driver_6_out_2, tri_led_driver_6_out_3,
       tri_led_driver_6_out_4, tri_led_driver_7_out_2, tri_led_driver_7_out_3, tri_led_driver_7_out_4,
       tri_led_driver_8_out_2, tri_led_driver_8_out_3, tri_led_driver_8_out_4, tri_led_driver_9_out_2,
       tri_led_driver_9_out_3, tri_led_driver_9_out_4, tri_led_driver_10_out_2, tri_led_driver_10_out_3,
       tri_led_driver_10_out_4, tri_led_driver_11_out_2, tri_led_driver_11_out_3, tri_led_driver_11_out_4,
       tri_led_driver_12_out_2, tri_led_driver_12_out_3, tri_led_driver_12_out_4, tri_led_driver_13_out_2,
       tri_led_driver_13_out_3, tri_led_driver_13_out_4, tri_led_driver_14_out_2, tri_led_driver_14_out_3,
       tri_led_driver_14_out_4, tri_led_driver_15_out_2, tri_led_driver_15_out_3, tri_led_driver_15_out_4,
       tri_led_driver_16_out_2, tri_led_driver_16_out_3, tri_led_driver_16_out_4, tri_led_driver_17_out_2,
       tri_led_driver_17_out_3, tri_led_driver_17_out_4, tri_led_driver_18_out_2, tri_led_driver_18_out_3,
       tri_led_driver_18_out_4, tri_led_driver_19_out_2, tri_led_driver_19_out_3, tri_led_driver_19_out_4,
       tri_led_driver_20_out_2, tri_led_driver_20_out_3, tri_led_driver_20_out_4, tri_led_driver_21_out_2,
       tri_led_driver_21_out_3, tri_led_driver_21_out_4, tri_led_driver_22_out_2, tri_led_driver_22_out_3,
       tri_led_driver_22_out_4, tri_led_driver_23_out_2, tri_led_driver_23_out_3, tri_led_driver_23_out_4,
       tri_led_driver_24_out_2, tri_led_driver_24_out_3, tri_led_driver_24_out_4, tri_led_driver_25_out_2,
       tri_led_driver_25_out_3, tri_led_driver_25_out_4, tri_led_driver_26_out_2, tri_led_driver_26_out_3,
       tri_led_driver_26_out_4, tri_led_driver_27_out_2, tri_led_driver_27_out_3, tri_led_driver_27_out_4,
       tri_led_driver_28_out_2, tri_led_driver_28_out_3, tri_led_driver_28_out_4, tri_led_driver_29_out_2,
       tri_led_driver_29_out_3, tri_led_driver_29_out_4, tri_led_driver_30_out_2, tri_led_driver_30_out_3,
       tri_led_driver_30_out_4, tri_led_driver_31_out_2, tri_led_driver_31_out_3, tri_led_driver_31_out_4;
  wire [0:0] button_1_out, clock_1_out;
  wire [1:0] cd_cycle_down_1_jo1____1jo, cu_cycle_up_1_jo1____o1j, d_latch_level_triggered_1_q,
       n0_constant_trit_1__0_constant, n1_constant_trit_1_minus_1_constant, n1_constant_trit_2__1_constant,
       nti_negative_trinary_inverter_1_jo1____1jj, pti_positive_trinary_inverter_1_jo1____11j,
       register_master_slave_d_latch_1_q, sti_simple_ternary_inverter_1_jo1____1oj,
       sti_simple_ternary_inverter_2_jo1____1oj, sti_simple_ternary_inverter_3_jo1____1oj,
       tnand_3_input_1_out_4, tnand_3_input_2_out_4, tnor_3_input_1_out_4, tnor_3_input_2_out_4;
  wire [11:0] keyboard_input_1_out_10, n6t_counter_w_async_reset_1_out;

  Button _2 (.out(_2_out));
  Button A (.out(A_out));
  Button D (.out(D_out));
  Button button_1 (.out(button_1_out[0]));
  _7_Segment_Display u_7_segment_display_1 ();  // open: g, f, a, b, e, d, c, dp
  keyboard_input keyboard_input_1 (
    .in_1(_2_out), .in_2(_3_out), .in_3(_4_out), .in_4(A_out), .in_5(_0_out), .in_6(_1_out), .in_7(D_out),
    .in_8(C_out), .in_9(B_out), .out_10(keyboard_input_1_out_10));
  Button _3 (.out(_3_out));
  Button _4 (.out(_4_out));
  Button _1 (.out(_1_out));
  Button _0 (.out(_0_out));
  Button B (.out(B_out));
  Button C (.out(C_out));
  _7_Segment_Display u_7_segment_display_2 (
    .g(n2t_to_7seg_driver_1_out_3), .f(n2t_to_7seg_driver_1_out_4), .a(n2t_to_7seg_driver_1_out_9),
    .b(n2t_to_7seg_driver_1_out_8), .e(n2t_to_7seg_driver_1_out_5), .d(n2t_to_7seg_driver_1_out_6),
    .c(n2t_to_7seg_driver_1_out_7), .dp(n2t_to_7seg_driver_1_out_2));
  _7_Segment_Display u_7_segment_display_3 (
    .g(n2t_to_7seg_driver_2_out_3), .f(n2t_to_7seg_driver_2_out_4), .a(n2t_to_7seg_driver_2_out_9),
    .b(n2t_to_7seg_driver_2_out_8), .e(n2t_to_7seg_driver_2_out_5), .d(n2t_to_7seg_driver_2_out_6),
    .c(n2t_to_7seg_driver_2_out_7), .dp(n2t_to_7seg_driver_2_out_2));
  _2t_to_7seg_driver u_2t_to_7seg_driver_1 (
    .in_1(keyboard_input_1_out_10[11:8]), .out_2(n2t_to_7seg_driver_1_out_2),
    .out_3(n2t_to_7seg_driver_1_out_3), .out_4(n2t_to_7seg_driver_1_out_4),
    .out_5(n2t_to_7seg_driver_1_out_5), .out_6(n2t_to_7seg_driver_1_out_6),
    .out_7(n2t_to_7seg_driver_1_out_7), .out_8(n2t_to_7seg_driver_1_out_8), .out_9(n2t_to_7seg_driver_1_out_9));
  LED led_1 (.in(tri_led_driver_1_out_2));
  LED led_2 (.in(tri_led_driver_2_out_2));
  LED led_3 (.in(tri_led_driver_6_out_2));
  tri_led_driver tri_led_driver_1 (
    .in_1(keyboard_input_1_out_10[11:10]), .out_2(tri_led_driver_1_out_2), .out_3(tri_led_driver_1_out_3),
    .out_4(tri_led_driver_1_out_4));
  LED led_4 (.in(tri_led_driver_2_out_3));
  LED led_5 (.in(tri_led_driver_1_out_3));
  tri_led_driver tri_led_driver_2 (
    .in_1(keyboard_input_1_out_10[9:8]), .out_2(tri_led_driver_2_out_2), .out_3(tri_led_driver_2_out_3),
    .out_4(tri_led_driver_2_out_4));
  LED led_6 (.in(tri_led_driver_6_out_4));
  LED led_7 (.in(tri_led_driver_2_out_4));
  LED led_8 (.in(tri_led_driver_1_out_4));
  Clock clock_1 (.out(clock_1_out[0]));
  LED led_9 (.in(tri_led_driver_3_out_2));
  D_Latch__level_triggered d_latch_level_triggered_1 (
    .D(keyboard_input_1_out_10[1:0]), .E_1({1'b0, button_1_out[0]}), .Q(d_latch_level_triggered_1_q));
  LED led_10 (.in(tri_led_driver_3_out_3));
  tri_led_driver tri_led_driver_3 (
    .in_1(d_latch_level_triggered_1_q), .out_2(tri_led_driver_3_out_2), .out_3(tri_led_driver_3_out_3),
    .out_4(tri_led_driver_3_out_4));
  LED led_11 (.in(tri_led_driver_3_out_4));
  _7_Segment_Display u_7_segment_display_4 (
    .g(n2t_to_7seg_driver_3_out_3), .f(n2t_to_7seg_driver_3_out_4), .a(n2t_to_7seg_driver_3_out_9),
    .b(n2t_to_7seg_driver_3_out_8), .e(n2t_to_7seg_driver_3_out_5), .d(n2t_to_7seg_driver_3_out_6),
    .c(n2t_to_7seg_driver_3_out_7), .dp(n2t_to_7seg_driver_3_out_2));
  _2t_to_7seg_driver u_2t_to_7seg_driver_2 (
    .in_1(keyboard_input_1_out_10[7:4]), .out_2(n2t_to_7seg_driver_2_out_2),
    .out_3(n2t_to_7seg_driver_2_out_3), .out_4(n2t_to_7seg_driver_2_out_4),
    .out_5(n2t_to_7seg_driver_2_out_5), .out_6(n2t_to_7seg_driver_2_out_6),
    .out_7(n2t_to_7seg_driver_2_out_7), .out_8(n2t_to_7seg_driver_2_out_8), .out_9(n2t_to_7seg_driver_2_out_9));
  LED led_12 (.in(tri_led_driver_5_out_2));
  LED led_13 (.in(tri_led_driver_4_out_2));
  LED led_14 (.in(tri_led_driver_5_out_3));
  LED led_15 (.in(tri_led_driver_6_out_3));
  tri_led_driver tri_led_driver_4 (
    .in_1(keyboard_input_1_out_10[5:4]), .out_2(tri_led_driver_4_out_2), .out_3(tri_led_driver_4_out_3),
    .out_4(tri_led_driver_4_out_4));
  tri_led_driver tri_led_driver_5 (
    .in_1(keyboard_input_1_out_10[3:2]), .out_2(tri_led_driver_5_out_2), .out_3(tri_led_driver_5_out_3),
    .out_4(tri_led_driver_5_out_4));
  tri_led_driver tri_led_driver_6 (
    .in_1(keyboard_input_1_out_10[7:6]), .out_2(tri_led_driver_6_out_2), .out_3(tri_led_driver_6_out_3),
    .out_4(tri_led_driver_6_out_4));
  LED led_16 (.in(tri_led_driver_4_out_3));
  LED led_17 (.in(tri_led_driver_5_out_4));
  LED led_18 (.in(tri_led_driver_4_out_4));
  _6t_counter_w_async_reset u_6t_counter_w_async_reset_1 (
    .clock({1'b0, clock_1_out[0]}), .reset__async({1'b0, in_1}), .out(n6t_counter_w_async_reset_1_out));
  Register__master_slave_D_latch register_master_slave_d_latch_1 (
    .Clock__pulse__latch_in_on_rising_edge__out_on_falling({1'b0, button_1_out[0]}),
    .D(keyboard_input_1_out_10[1:0]), .Q(register_master_slave_d_latch_1_q));
  _2t_to_7seg_driver u_2t_to_7seg_driver_3 (
    .in_1(keyboard_input_1_out_10[3:0]), .out_2(n2t_to_7seg_driver_3_out_2),
    .out_3(n2t_to_7seg_driver_3_out_3), .out_4(n2t_to_7seg_driver_3_out_4),
    .out_5(n2t_to_7seg_driver_3_out_5), .out_6(n2t_to_7seg_driver_3_out_6),
    .out_7(n2t_to_7seg_driver_3_out_7), .out_8(n2t_to_7seg_driver_3_out_8), .out_9(n2t_to_7seg_driver_3_out_9));
  LED led_19 (.in(tri_led_driver_7_out_2));
  tri_led_driver tri_led_driver_7 (
    .in_1(keyboard_input_1_out_10[1:0]), .out_2(tri_led_driver_7_out_2), .out_3(tri_led_driver_7_out_3),
    .out_4(tri_led_driver_7_out_4));
  LED led_20 (.in(tri_led_driver_7_out_3));
  LED led_21 (.in(tri_led_driver_7_out_4));
  LED led_22 (.in(tri_led_driver_8_out_2));
  LED led_23 (.in(tri_led_driver_8_out_3));
  tri_led_driver tri_led_driver_8 (
    .in_1(keyboard_input_1_out_10[5:4]), .out_2(tri_led_driver_8_out_2), .out_3(tri_led_driver_8_out_3),
    .out_4(tri_led_driver_8_out_4));
  LED led_24 (.in(tri_led_driver_8_out_4));
  LED led_25 (.in(tri_led_driver_9_out_2));
  LED led_26 (.in(tri_led_driver_9_out_3));
  tri_led_driver tri_led_driver_9 (
    .in_1(register_master_slave_d_latch_1_q), .out_2(tri_led_driver_9_out_2), .out_3(tri_led_driver_9_out_3),
    .out_4(tri_led_driver_9_out_4));
  LED led_27 (.in(tri_led_driver_9_out_4));
  _7_Segment_Display u_7_segment_display_5 (
    .g(n2t_to_7seg_driver_6_out_3), .f(n2t_to_7seg_driver_6_out_4), .a(n2t_to_7seg_driver_6_out_9),
    .b(n2t_to_7seg_driver_6_out_8), .e(n2t_to_7seg_driver_6_out_5), .d(n2t_to_7seg_driver_6_out_6),
    .c(n2t_to_7seg_driver_6_out_7), .dp(n2t_to_7seg_driver_6_out_2));
  _7_Segment_Display u_7_segment_display_6 (
    .g(n2t_to_7seg_driver_4_out_3), .f(n2t_to_7seg_driver_4_out_4), .a(n2t_to_7seg_driver_4_out_9),
    .b(n2t_to_7seg_driver_4_out_8), .e(n2t_to_7seg_driver_4_out_5), .d(n2t_to_7seg_driver_4_out_6),
    .c(n2t_to_7seg_driver_4_out_7), .dp(n2t_to_7seg_driver_4_out_2));
  _2t_to_7seg_driver u_2t_to_7seg_driver_4 (
    .in_1(n6t_counter_w_async_reset_1_out[11:8]), .out_2(n2t_to_7seg_driver_4_out_2),
    .out_3(n2t_to_7seg_driver_4_out_3), .out_4(n2t_to_7seg_driver_4_out_4),
    .out_5(n2t_to_7seg_driver_4_out_5), .out_6(n2t_to_7seg_driver_4_out_6),
    .out_7(n2t_to_7seg_driver_4_out_7), .out_8(n2t_to_7seg_driver_4_out_8), .out_9(n2t_to_7seg_driver_4_out_9));
  LED led_28 (.in(tri_led_driver_12_out_2));
  LED led_29 (.in(tri_led_driver_10_out_2));
  LED led_30 (.in(tri_led_driver_11_out_2));
  tri_led_driver tri_led_driver_10 (
    .in_1(n6t_counter_w_async_reset_1_out[9:8]), .out_2(tri_led_driver_10_out_2),
    .out_3(tri_led_driver_10_out_3), .out_4(tri_led_driver_10_out_4));
  tri_led_driver tri_led_driver_11 (
    .in_1(n6t_counter_w_async_reset_1_out[11:10]), .out_2(tri_led_driver_11_out_2),
    .out_3(tri_led_driver_11_out_3), .out_4(tri_led_driver_11_out_4));
  tri_led_driver tri_led_driver_12 (
    .in_1(n6t_counter_w_async_reset_1_out[7:6]), .out_2(tri_led_driver_12_out_2),
    .out_3(tri_led_driver_12_out_3), .out_4(tri_led_driver_12_out_4));
  LED led_31 (.in(tri_led_driver_11_out_3));
  LED led_32 (.in(tri_led_driver_10_out_3));
  LED led_33 (.in(tri_led_driver_12_out_3));
  LED led_34 (.in(tri_led_driver_10_out_4));
  LED led_35 (.in(tri_led_driver_11_out_4));
  LED led_36 (.in(tri_led_driver_12_out_4));
  LED led_37 (.in(tri_led_driver_13_out_2));
  LED led_38 (.in(tri_led_driver_13_out_3));
  tri_led_driver tri_led_driver_13 (
    .in_1(keyboard_input_1_out_10[1:0]), .out_2(tri_led_driver_13_out_2), .out_3(tri_led_driver_13_out_3),
    .out_4(tri_led_driver_13_out_4));
  LED led_39 (.in(tri_led_driver_13_out_4));
  _7_Segment_Display u_7_segment_display_7 (
    .g(n2t_to_7seg_driver_5_out_3), .f(n2t_to_7seg_driver_5_out_4), .a(n2t_to_7seg_driver_5_out_9),
    .b(n2t_to_7seg_driver_5_out_8), .e(n2t_to_7seg_driver_5_out_5), .d(n2t_to_7seg_driver_5_out_6),
    .c(n2t_to_7seg_driver_5_out_7), .dp(n2t_to_7seg_driver_5_out_2));
  _2t_to_7seg_driver u_2t_to_7seg_driver_5 (
    .in_1(n6t_counter_w_async_reset_1_out[3:0]), .out_2(n2t_to_7seg_driver_5_out_2),
    .out_3(n2t_to_7seg_driver_5_out_3), .out_4(n2t_to_7seg_driver_5_out_4),
    .out_5(n2t_to_7seg_driver_5_out_5), .out_6(n2t_to_7seg_driver_5_out_6),
    .out_7(n2t_to_7seg_driver_5_out_7), .out_8(n2t_to_7seg_driver_5_out_8), .out_9(n2t_to_7seg_driver_5_out_9));
  _2t_to_7seg_driver u_2t_to_7seg_driver_6 (
    .in_1(n6t_counter_w_async_reset_1_out[7:4]), .out_2(n2t_to_7seg_driver_6_out_2),
    .out_3(n2t_to_7seg_driver_6_out_3), .out_4(n2t_to_7seg_driver_6_out_4),
    .out_5(n2t_to_7seg_driver_6_out_5), .out_6(n2t_to_7seg_driver_6_out_6),
    .out_7(n2t_to_7seg_driver_6_out_7), .out_8(n2t_to_7seg_driver_6_out_8), .out_9(n2t_to_7seg_driver_6_out_9));
  LED led_40 (.in(tri_led_driver_16_out_2));
  LED led_41 (.in(tri_led_driver_15_out_2));
  LED led_42 (.in(tri_led_driver_14_out_2));
  tri_led_driver tri_led_driver_14 (
    .in_1(n6t_counter_w_async_reset_1_out[3:2]), .out_2(tri_led_driver_14_out_2),
    .out_3(tri_led_driver_14_out_3), .out_4(tri_led_driver_14_out_4));
  tri_led_driver tri_led_driver_15 (
    .in_1(n6t_counter_w_async_reset_1_out[5:4]), .out_2(tri_led_driver_15_out_2),
    .out_3(tri_led_driver_15_out_3), .out_4(tri_led_driver_15_out_4));
  LED led_43 (.in(tri_led_driver_15_out_3));
  LED led_44 (.in(tri_led_driver_14_out_3));
  LED led_45 (.in(tri_led_driver_16_out_4));
  LED led_46 (.in(tri_led_driver_14_out_4));
  LED led_47 (.in(tri_led_driver_15_out_4));
  CU_Cycle_Up cu_cycle_up_1 (.in_1(keyboard_input_1_out_10[1:0]), .jo1____o1j(cu_cycle_up_1_jo1____o1j));
  CD_Cycle_Down cd_cycle_down_1 (.in_1(keyboard_input_1_out_10[1:0]), .jo1____1jo(cd_cycle_down_1_jo1____1jo));
  TNAND_3_input tnand_3_input_1 (
    .in_1(keyboard_input_1_out_10[1:0]), .in_2(keyboard_input_1_out_10[1:0]),
    .in_3(keyboard_input_1_out_10[1:0]), .out_4(tnand_3_input_1_out_4));
  TNOR_3_input tnor_3_input_1 (
    .in_1(keyboard_input_1_out_10[1:0]), .in_2(keyboard_input_1_out_10[1:0]),
    .in_3(keyboard_input_1_out_10[1:0]), .out_4(tnor_3_input_1_out_4));
  TNOR_3_input tnor_3_input_2 (
    .in_1(keyboard_input_1_out_10[1:0]), .in_2(keyboard_input_1_out_10[1:0]),
    .in_3(keyboard_input_1_out_10[5:4]), .out_4(tnor_3_input_2_out_4));
  TNAND_3_input tnand_3_input_2 (
    .in_1(keyboard_input_1_out_10[1:0]), .in_2(keyboard_input_1_out_10[1:0]),
    .in_3(keyboard_input_1_out_10[5:4]), .out_4(tnand_3_input_2_out_4));
  tri_led_driver tri_led_driver_16 (
    .in_1(n6t_counter_w_async_reset_1_out[1:0]), .out_2(tri_led_driver_16_out_2),
    .out_3(tri_led_driver_16_out_3), .out_4(tri_led_driver_16_out_4));
  LED led_48 (.in(tri_led_driver_16_out_3));
  LED led_49 (.in(tri_led_driver_17_out_2));
  LED led_50 (.in(tri_led_driver_17_out_3));
  tri_led_driver tri_led_driver_17 (
    .in_1(n1_constant_trit_1_minus_1_constant), .out_2(tri_led_driver_17_out_2),
    .out_3(tri_led_driver_17_out_3), .out_4(tri_led_driver_17_out_4));
  _1_Constant_Trit_2 u_1_constant_trit_1 (.minus_1_constant(n1_constant_trit_1_minus_1_constant));
  LED led_51 (.in(tri_led_driver_17_out_4));
  LED led_52 (.in(tri_led_driver_18_out_2));
  tri_led_driver tri_led_driver_18 (
    .in_1(cu_cycle_up_1_jo1____o1j), .out_2(tri_led_driver_18_out_2), .out_3(tri_led_driver_18_out_3),
    .out_4(tri_led_driver_18_out_4));
  LED led_53 (.in(tri_led_driver_18_out_3));
  LED led_54 (.in(tri_led_driver_18_out_4));
  LED led_55 (.in(tri_led_driver_19_out_2));
  tri_led_driver tri_led_driver_19 (
    .in_1(cd_cycle_down_1_jo1____1jo), .out_2(tri_led_driver_19_out_2), .out_3(tri_led_driver_19_out_3),
    .out_4(tri_led_driver_19_out_4));
  LED led_56 (.in(tri_led_driver_19_out_3));
  LED led_57 (.in(tri_led_driver_19_out_4));
  LED led_58 (.in(tri_led_driver_20_out_2));
  LED led_59 (.in(tri_led_driver_20_out_3));
  tri_led_driver tri_led_driver_20 (
    .in_1(tnand_3_input_1_out_4), .out_2(tri_led_driver_20_out_2), .out_3(tri_led_driver_20_out_3),
    .out_4(tri_led_driver_20_out_4));
  LED led_60 (.in(tri_led_driver_20_out_4));
  LED led_61 (.in(tri_led_driver_21_out_2));
  tri_led_driver tri_led_driver_21 (
    .in_1(tnor_3_input_1_out_4), .out_2(tri_led_driver_21_out_2), .out_3(tri_led_driver_21_out_3),
    .out_4(tri_led_driver_21_out_4));
  LED led_62 (.in(tri_led_driver_21_out_3));
  LED led_63 (.in(tri_led_driver_21_out_4));
  LED led_64 (.in(tri_led_driver_22_out_2));
  LED led_65 (.in(tri_led_driver_22_out_3));
  tri_led_driver tri_led_driver_22 (
    .in_1(tnor_3_input_2_out_4), .out_2(tri_led_driver_22_out_2), .out_3(tri_led_driver_22_out_3),
    .out_4(tri_led_driver_22_out_4));
  LED led_66 (.in(tri_led_driver_22_out_4));
  LED led_67 (.in(tri_led_driver_23_out_2));
  LED led_68 (.in(tri_led_driver_23_out_3));
  tri_led_driver tri_led_driver_23 (
    .in_1(tnand_3_input_2_out_4), .out_2(tri_led_driver_23_out_2), .out_3(tri_led_driver_23_out_3),
    .out_4(tri_led_driver_23_out_4));
  LED led_69 (.in(tri_led_driver_23_out_4));
  LED led_70 (.in(tri_led_driver_24_out_2));
  LED led_71 (.in(tri_led_driver_24_out_3));
  tri_led_driver tri_led_driver_24 (
    .in_1(n0_constant_trit_1__0_constant), .out_2(tri_led_driver_24_out_2), .out_3(tri_led_driver_24_out_3),
    .out_4(tri_led_driver_24_out_4));
  _0_Constant_Trit u_0_constant_trit_1 (._0_constant(n0_constant_trit_1__0_constant));
  LED led_72 (.in(tri_led_driver_24_out_4));
  PTI_Positive_Trinary_Inverter pti_positive_trinary_inverter_1 (
    .in_1(keyboard_input_1_out_10[1:0]), .jo1____11j(pti_positive_trinary_inverter_1_jo1____11j));
  STI_Simple_Ternary_Inverter sti_simple_ternary_inverter_1 (
    .in_1(keyboard_input_1_out_10[1:0]), .jo1____1oj(sti_simple_ternary_inverter_1_jo1____1oj));
  NTI_Negative_Trinary_Inverter nti_negative_trinary_inverter_1 (
    .in_1(keyboard_input_1_out_10[1:0]), .jo1____1jj(nti_negative_trinary_inverter_1_jo1____1jj));
  STI_Simple_Ternary_Inverter sti_simple_ternary_inverter_2 (
    .in_1(tnor_3_input_2_out_4), .jo1____1oj(sti_simple_ternary_inverter_2_jo1____1oj));
  STI_Simple_Ternary_Inverter sti_simple_ternary_inverter_3 (
    .in_1(tnand_3_input_2_out_4), .jo1____1oj(sti_simple_ternary_inverter_3_jo1____1oj));
  LED led_73 (.in(tri_led_driver_25_out_2));
  _1_Constant_Trit u_1_constant_trit_2 (._1_constant(n1_constant_trit_2__1_constant));
  tri_led_driver tri_led_driver_25 (
    .in_1(n1_constant_trit_2__1_constant), .out_2(tri_led_driver_25_out_2), .out_3(tri_led_driver_25_out_3),
    .out_4(tri_led_driver_25_out_4));
  LED led_74 (.in(tri_led_driver_25_out_3));
  LED led_75 (.in(tri_led_driver_25_out_4));
  LED led_76 (.in(tri_led_driver_26_out_2));
  tri_led_driver tri_led_driver_26 (
    .in_1(keyboard_input_1_out_10[1:0]), .out_2(tri_led_driver_26_out_2), .out_3(tri_led_driver_26_out_3),
    .out_4(tri_led_driver_26_out_4));
  LED led_77 (.in(tri_led_driver_26_out_3));
  LED led_78 (.in(tri_led_driver_26_out_4));
  LED led_79 (.in(tri_led_driver_27_out_2));
  LED led_80 (.in(tri_led_driver_27_out_3));
  tri_led_driver tri_led_driver_27 (
    .in_1(pti_positive_trinary_inverter_1_jo1____11j), .out_2(tri_led_driver_27_out_2),
    .out_3(tri_led_driver_27_out_3), .out_4(tri_led_driver_27_out_4));
  LED led_81 (.in(tri_led_driver_27_out_4));
  LED led_82 (.in(tri_led_driver_28_out_2));
  tri_led_driver tri_led_driver_28 (
    .in_1(sti_simple_ternary_inverter_1_jo1____1oj), .out_2(tri_led_driver_28_out_2),
    .out_3(tri_led_driver_28_out_3), .out_4(tri_led_driver_28_out_4));
  LED led_83 (.in(tri_led_driver_28_out_3));
  LED led_84 (.in(tri_led_driver_28_out_4));
  LED led_85 (.in(tri_led_driver_29_out_2));
  LED led_86 (.in(tri_led_driver_29_out_3));
  tri_led_driver tri_led_driver_29 (
    .in_1(nti_negative_trinary_inverter_1_jo1____1jj), .out_2(tri_led_driver_29_out_2),
    .out_3(tri_led_driver_29_out_3), .out_4(tri_led_driver_29_out_4));
  LED led_87 (.in(tri_led_driver_29_out_4));
  LED led_88 (.in(tri_led_driver_30_out_2));
  LED led_89 (.in(tri_led_driver_30_out_3));
  tri_led_driver tri_led_driver_30 (
    .in_1(sti_simple_ternary_inverter_2_jo1____1oj), .out_2(tri_led_driver_30_out_2),
    .out_3(tri_led_driver_30_out_3), .out_4(tri_led_driver_30_out_4));
  LED led_90 (.in(tri_led_driver_30_out_4));
  LED led_91 (.in(tri_led_driver_31_out_2));
  LED led_92 (.in(tri_led_driver_31_out_3));
  tri_led_driver tri_led_driver_31 (
    .in_1(sti_simple_ternary_inverter_3_jo1____1oj), .out_2(tri_led_driver_31_out_2),
    .out_3(tri_led_driver_31_out_3), .out_4(tri_led_driver_31_out_4));
  LED led_93 (.in(tri_led_driver_31_out_4));
endmodule

module calculator_example (
);

  wire _0_out, _1_out, _2_out, _3_out, _4_out, A_out, B_out, button_out, C_out, D_out, Enter_out,
       n2t_to_7seg_driver_1_out_2, n2t_to_7seg_driver_1_out_3, n2t_to_7seg_driver_1_out_4,
       n2t_to_7seg_driver_1_out_5, n2t_to_7seg_driver_1_out_6, n2t_to_7seg_driver_1_out_7,
       n2t_to_7seg_driver_1_out_8, n2t_to_7seg_driver_1_out_9, n2t_to_7seg_driver_2_out_2,
       n2t_to_7seg_driver_2_out_3, n2t_to_7seg_driver_2_out_4, n2t_to_7seg_driver_2_out_5,
       n2t_to_7seg_driver_2_out_6, n2t_to_7seg_driver_2_out_7, n2t_to_7seg_driver_2_out_8,
       n2t_to_7seg_driver_2_out_9, n2t_to_7seg_driver_3_out_2, n2t_to_7seg_driver_3_out_3,
       n2t_to_7seg_driver_3_out_4, n2t_to_7seg_driver_3_out_5, n2t_to_7seg_driver_3_out_6,
       n2t_to_7seg_driver_3_out_7, n2t_to_7seg_driver_3_out_8, n2t_to_7seg_driver_3_out_9,
       n2t_to_7seg_driver_4_out_2, n2t_to_7seg_driver_4_out_3, n2t_to_7seg_driver_4_out_4,
       n2t_to_7seg_driver_4_out_5, n2t_to_7seg_driver_4_out_6, n2t_to_7seg_driver_4_out_7,
       n2t_to_7seg_driver_4_out_8, n2t_to_7seg_driver_4_out_9, n2t_to_7seg_driver_5_out_2,
       n2t_to_7seg_driver_5_out_3, n2t_to_7seg_driver_5_out_4, n2t_to_7seg_driver_5_out_5,
       n2t_to_7seg_driver_5_out_6, n2t_to_7seg_driver_5_out_7, n2t_to_7seg_driver_5_out_8,
       n2t_to_7seg_driver_5_out_9, n2t_to_7seg_driver_6_out_2, n2t_to_7seg_driver_6_out_3,
       n2t_to_7seg_driver_6_out_4, n2t_to_7seg_driver_6_out_5, n2t_to_7seg_driver_6_out_6,
       n2t_to_7seg_driver_6_out_7, n2t_to_7seg_driver_6_out_8, n2t_to_7seg_driver_6_out_9,
       n2t_to_7seg_driver_7_out_2, n2t_to_7seg_driver_7_out_3, n2t_to_7seg_driver_7_out_4,
       n2t_to_7seg_driver_7_out_5, n2t_to_7seg_driver_7_out_6, n2t_to_7seg_driver_7_out_7,
       n2t_to_7seg_driver_7_out_8, n2t_to_7seg_driver_7_out_9, n2t_to_7seg_driver_8_out_2,
       n2t_to_7seg_driver_8_out_3, n2t_to_7seg_driver_8_out_4, n2t_to_7seg_driver_8_out_5,
       n2t_to_7seg_driver_8_out_6, n2t_to_7seg_driver_8_out_7, n2t_to_7seg_driver_8_out_8,
       n2t_to_7seg_driver_8_out_9, n2t_to_7seg_driver_9_out_2, n2t_to_7seg_driver_9_out_3,
       n2t_to_7seg_driver_9_out_4, n2t_to_7seg_driver_9_out_5, n2t_to_7seg_driver_9_out_6,
       n2t_to_7seg_driver_9_out_7, n2t_to_7seg_driver_9_out_8, n2t_to_7seg_driver_9_out_9,
       n2t_to_7seg_driver_10_out_2, n2t_to_7seg_driver_10_out_3, n2t_to_7seg_driver_10_out_4,
       n2t_to_7seg_driver_10_out_5, n2t_to_7seg_driver_10_out_6, n2t_to_7seg_driver_10_out_7,
       n2t_to_7seg_driver_10_out_8, n2t_to_7seg_driver_10_out_9, n2t_to_7seg_driver_11_out_2,
       n2t_to_7seg_driver_11_out_3, n2t_to_7seg_driver_11_out_4, n2t_to_7seg_driver_11_out_5,
       n2t_to_7seg_driver_11_out_6, n2t_to_7seg_driver_11_out_7, n2t_to_7seg_driver_11_out_8,
       n2t_to_7seg_driver_11_out_9, n2t_to_7seg_driver_12_out_2, n2t_to_7seg_driver_12_out_3,
       n2t_to_7seg_driver_12_out_4, n2t_to_7seg_driver_12_out_5, n2t_to_7seg_driver_12_out_6,
       n2t_to_7seg_driver_12_out_7, n2t_to_7seg_driver_12_out_8, n2t_to_7seg_driver_12_out_9,
       n2t_to_7seg_driver_13_out_2, n2t_to_7seg_driver_13_out_3, n2t_to_7seg_driver_13_out_4,
       n2t_to_7seg_driver_13_out_5, n2t_to_7seg_driver_13_out_6, n2t_to_7seg_driver_13_out_7,
       n2t_to_7seg_driver_13_out_8, n2t_to_7seg_driver_13_out_9, n2t_to_7seg_driver_14_out_2,
       n2t_to_7seg_driver_14_out_3, n2t_to_7seg_driver_14_out_4, n2t_to_7seg_driver_14_out_5,
       n2t_to_7seg_driver_14_out_6, n2t_to_7seg_driver_14_out_7, n2t_to_7seg_driver_14_out_8,
       n2t_to_7seg_driver_14_out_9, n2t_to_7seg_driver_15_out_2, n2t_to_7seg_driver_15_out_3,
       n2t_to_7seg_driver_15_out_4, n2t_to_7seg_driver_15_out_5, n2t_to_7seg_driver_15_out_6,
       n2t_to_7seg_driver_15_out_7, n2t_to_7seg_driver_15_out_8, n2t_to_7seg_driver_15_out_9,
       n2t_to_7seg_driver_16_out_2, n2t_to_7seg_driver_16_out_3, n2t_to_7seg_driver_16_out_4,
       n2t_to_7seg_driver_16_out_5, n2t_to_7seg_driver_16_out_6, n2t_to_7seg_driver_16_out_7,
       n2t_to_7seg_driver_16_out_8, n2t_to_7seg_driver_16_out_9, n2t_to_7seg_driver_17_out_2,
       n2t_to_7seg_driver_17_out_3, n2t_to_7seg_driver_17_out_4, n2t_to_7seg_driver_17_out_5,
       n2t_to_7seg_driver_17_out_6, n2t_to_7seg_driver_17_out_7, n2t_to_7seg_driver_17_out_8,
       n2t_to_7seg_driver_17_out_9, n2t_to_7seg_driver_18_out_2, n2t_to_7seg_driver_18_out_3,
       n2t_to_7seg_driver_18_out_4, n2t_to_7seg_driver_18_out_5, n2t_to_7seg_driver_18_out_6,
       n2t_to_7seg_driver_18_out_7, n2t_to_7seg_driver_18_out_8, n2t_to_7seg_driver_18_out_9, neg_out,
       tri_led_driver_1_out_2, tri_led_driver_1_out_3, tri_led_driver_1_out_4, tri_led_driver_2_out_2,
       tri_led_driver_2_out_3, tri_led_driver_2_out_4, tri_led_driver_3_out_2, tri_led_driver_3_out_3,
       tri_led_driver_3_out_4, tri_led_driver_4_out_2, tri_led_driver_4_out_3, tri_led_driver_4_out_4,
       tri_led_driver_5_out_2, tri_led_driver_5_out_3, tri_led_driver_5_out_4, tri_led_driver_6_out_2,
       tri_led_driver_6_out_3, tri_led_driver_6_out_4, tri_led_driver_7_out_2, tri_led_driver_7_out_3,
       tri_led_driver_7_out_4;
  wire [0:0] or_9_out;
  wire [1:0] cu_cycle_up_1_jo1____o1j, cu_cycle_up_2_jo1____o1j, cu_cycle_up_3_jo1____o1j,
       cu_cycle_up_4_jo1____o1j, cu_cycle_up_5_jo1____o1j, cu_cycle_up_6_jo1____o1j,
       cu_cycle_up_7_jo1____o1j, cu_cycle_up_8_jo1____o1j, cu_cycle_up_9_jo1____o1j,
       cu_cycle_up_10_jo1____o1j, cu_cycle_up_11_jo1____o1j, cu_cycle_up_12_jo1____o1j,
       d_latch_level_triggered_1_q, d_latch_level_triggered_2_q, d_latch_level_triggered_3_q,
       d_latch_level_triggered_4_q, n0_constant_trit_1__0_constant, n6t_ripple_carry_adder_1_out_5, or_2_out,
       or_4_out, or_5_out, or_8_out, pti_positive_trinary_inverter_1_jo1____11j, tor_max_3_input_1_out_4;
  wire [3:0] n6t_register_1_q;
  wire [11:0] keyboard_input_1_out_10, n6t_3_1_mux_1_out_5, n6t_3_1_mux_2_out_5, n6t_3_1_mux_3_out_5,
       n6t_register_2_q, n6t_ripple_carry_adder_1_out_4, n6t_sti_1_out_6x___jo1____10j,
       n6t_x_18_stack_1_top_of_stack;
  wire [11:4] n6t_register_1_q_2;

  _0_Constant_Trit u_0_constant_trit_1 (._0_constant(n0_constant_trit_1__0_constant));
  _6t_ripple_carry_adder u_6t_ripple_carry_adder_1 (
    .in_1(n6t_register_2_q), .in_2({n6t_register_1_q_2, n6t_register_1_q}),
    .in_3(n0_constant_trit_1__0_constant), .out_4(n6t_ripple_carry_adder_1_out_4),
    .out_5(n6t_ripple_carry_adder_1_out_5));
  _6t_STI u_6t_sti_1 (.in({n6t_register_1_q_2, n6t_register_1_q}), .out_6x___jo1____10j(n6t_sti_1_out_6x___jo1____10j));
  Button _2 (.out(_2_out));
  Button A (.out(A_out));
  Button D (.out(D_out));
  LED led_1 (.in(tri_led_driver_1_out_2));
  tri_led_driver tri_led_driver_1 (
    .in_1(n6t_ripple_carry_adder_1_out_5), .out_2(tri_led_driver_1_out_2), .out_3(tri_led_driver_1_out_3),
    .out_4(tri_led_driver_1_out_4));
  LED led_2 (.in(tri_led_driver_1_out_3));
  LED led_3 (.in(tri_led_driver_1_out_4));
  keyboard_input keyboard_input_1 (
    .in_1(_2_out), .in_2(_3_out), .in_3(_4_out), .in_4(A_out), .in_5(_0_out), .in_6(_1_out), .in_7(D_out),
    .in_8(C_out), .in_9(B_out), .out_10(keyboard_input_1_out_10));
  Button _3 (.out(_3_out));
  Button _4 (.out(_4_out));
  Button _0 (.out(_0_out));
  Button _1 (.out(_1_out));
  Button B (.out(B_out));
  Button C (.out(C_out));
  _7_Segment_Display u_7_segment_display_1 (
    .g(n2t_to_7seg_driver_4_out_3), .f(n2t_to_7seg_driver_4_out_4), .a(n2t_to_7seg_driver_4_out_9),
    .b(n2t_to_7seg_driver_4_out_8), .e(n2t_to_7seg_driver_4_out_5), .d(n2t_to_7seg_driver_4_out_6),
    .c(n2t_to_7seg_driver_4_out_7), .dp(n2t_to_7seg_driver_4_out_2));
  _7_Segment_Display u_7_segment_display_2 (
    .g(n2t_to_7seg_driver_1_out_3), .f(n2t_to_7seg_driver_1_out_4), .a(n2t_to_7seg_driver_1_out_9),
    .b(n2t_to_7seg_driver_1_out_8), .e(n2t_to_7seg_driver_1_out_5), .d(n2t_to_7seg_driver_1_out_6),
    .c(n2t_to_7seg_driver_1_out_7), .dp(n2t_to_7seg_driver_1_out_2));
  _2t_to_7seg_driver u_2t_to_7seg_driver_1 (
    .in_1(n6t_ripple_carry_adder_1_out_4[11:8]), .out_2(n2t_to_7seg_driver_1_out_2),
    .out_3(n2t_to_7seg_driver_1_out_3), .out_4(n2t_to_7seg_driver_1_out_4),
    .out_5(n2t_to_7seg_driver_1_out_5), .out_6(n2t_to_7seg_driver_1_out_6),
    .out_7(n2t_to_7seg_driver_1_out_7), .out_8(n2t_to_7seg_driver_1_out_8), .out_9(n2t_to_7seg_driver_1_out_9));
  _7_Segment_Display u_7_segment_display_3 (
    .g(n2t_to_7seg_driver_2_out_3), .f(n2t_to_7seg_driver_2_out_4), .a(n2t_to_7seg_driver_2_out_9),
    .b(n2t_to_7seg_driver_2_out_8), .e(n2t_to_7seg_driver_2_out_5), .d(n2t_to_7seg_driver_2_out_6),
    .c(n2t_to_7seg_driver_2_out_7), .dp(n2t_to_7seg_driver_2_out_2));
  _7_Segment_Display u_7_segment_display_4 (
    .g(n2t_to_7seg_driver_6_out_3), .f(n2t_to_7seg_driver_6_out_4), .a(n2t_to_7seg_driver_6_out_9),
    .b(n2t_to_7seg_driver_6_out_8), .e(n2t_to_7seg_driver_6_out_5), .d(n2t_to_7seg_driver_6_out_6),
    .c(n2t_to_7seg_driver_6_out_7), .dp(n2t_to_7seg_driver_6_out_2));
  _2t_to_7seg_driver u_2t_to_7seg_driver_2 (
    .in_1(n6t_sti_1_out_6x___jo1____10j[11:8]), .out_2(n2t_to_7seg_driver_2_out_2),
    .out_3(n2t_to_7seg_driver_2_out_3), .out_4(n2t_to_7seg_driver_2_out_4),
    .out_5(n2t_to_7seg_driver_2_out_5), .out_6(n2t_to_7seg_driver_2_out_6),
    .out_7(n2t_to_7seg_driver_2_out_7), .out_8(n2t_to_7seg_driver_2_out_8), .out_9(n2t_to_7seg_driver_2_out_9));
  _7_Segment_Display u_7_segment_display_5 (
    .g(n2t_to_7seg_driver_9_out_3), .f(n2t_to_7seg_driver_9_out_4), .a(n2t_to_7seg_driver_9_out_9),
    .b(n2t_to_7seg_driver_9_out_8), .e(n2t_to_7seg_driver_9_out_5), .d(n2t_to_7seg_driver_9_out_6),
    .c(n2t_to_7seg_driver_9_out_7), .dp(n2t_to_7seg_driver_9_out_2));
  _7_Segment_Display u_7_segment_display_6 (
    .g(n2t_to_7seg_driver_3_out_3), .f(n2t_to_7seg_driver_3_out_4), .a(n2t_to_7seg_driver_3_out_9),
    .b(n2t_to_7seg_driver_3_out_8), .e(n2t_to_7seg_driver_3_out_5), .d(n2t_to_7seg_driver_3_out_6),
    .c(n2t_to_7seg_driver_3_out_7), .dp(n2t_to_7seg_driver_3_out_2));
  _2t_to_7seg_driver u_2t_to_7seg_driver_3 (
    .in_1(keyboard_input_1_out_10[11:8]), .out_2(n2t_to_7seg_driver_3_out_2),
    .out_3(n2t_to_7seg_driver_3_out_3), .out_4(n2t_to_7seg_driver_3_out_4),
    .out_5(n2t_to_7seg_driver_3_out_5), .out_6(n2t_to_7seg_driver_3_out_6),
    .out_7(n2t_to_7seg_driver_3_out_7), .out_8(n2t_to_7seg_driver_3_out_8), .out_9(n2t_to_7seg_driver_3_out_9));
  LED led_4 (.in(tri_led_driver_4_out_2));
  LED led_5 (.in(tri_led_driver_3_out_2));
  LED led_6 (.in(tri_led_driver_2_out_2));
  LED led_7 (.in(tri_led_driver_4_out_3));
  tri_led_driver tri_led_driver_2 (
    .in_1(keyboard_input_1_out_10[9:8]), .out_2(tri_led_driver_2_out_2), .out_3(tri_led_driver_2_out_3),
    .out_4(tri_led_driver_2_out_4));
  tri_led_driver tri_led_driver_3 (
    .in_1(keyboard_input_1_out_10[7:6]), .out_2(tri_led_driver_3_out_2), .out_3(tri_led_driver_3_out_3),
    .out_4(tri_led_driver_3_out_4));
  LED led_8 (.in(tri_led_driver_2_out_3));
  LED led_9 (.in(tri_led_driver_3_out_3));
  tri_led_driver tri_led_driver_4 (
    .in_1(keyboard_input_1_out_10[11:10]), .out_2(tri_led_driver_4_out_2), .out_3(tri_led_driver_4_out_3),
    .out_4(tri_led_driver_4_out_4));
  LED led_10 (.in(tri_led_driver_3_out_4));
  LED led_11 (.in(tri_led_driver_4_out_4));
  LED led_12 (.in(tri_led_driver_2_out_4));
  _7_Segment_Display u_7_segment_display_7 (
    .g(n2t_to_7seg_driver_5_out_3), .f(n2t_to_7seg_driver_5_out_4), .a(n2t_to_7seg_driver_5_out_9),
    .b(n2t_to_7seg_driver_5_out_8), .e(n2t_to_7seg_driver_5_out_5), .d(n2t_to_7seg_driver_5_out_6),
    .c(n2t_to_7seg_driver_5_out_7), .dp(n2t_to_7seg_driver_5_out_2));
  _2t_to_7seg_driver u_2t_to_7seg_driver_4 (
    .in_1(n6t_ripple_carry_adder_1_out_4[7:4]), .out_2(n2t_to_7seg_driver_4_out_2),
    .out_3(n2t_to_7seg_driver_4_out_3), .out_4(n2t_to_7seg_driver_4_out_4),
    .out_5(n2t_to_7seg_driver_4_out_5), .out_6(n2t_to_7seg_driver_4_out_6),
    .out_7(n2t_to_7seg_driver_4_out_7), .out_8(n2t_to_7seg_driver_4_out_8), .out_9(n2t_to_7seg_driver_4_out_9));
  _2t_to_7seg_driver u_2t_to_7seg_driver_5 (
    .in_1(n6t_ripple_carry_adder_1_out_4[3:0]), .out_2(n2t_to_7seg_driver_5_out_2),
    .out_3(n2t_to_7seg_driver_5_out_3), .out_4(n2t_to_7seg_driver_5_out_4),
    .out_5(n2t_to_7seg_driver_5_out_5), .out_6(n2t_to_7seg_driver_5_out_6),
    .out_7(n2t_to_7seg_driver_5_out_7), .out_8(n2t_to_7seg_driver_5_out_8), .out_9(n2t_to_7seg_driver_5_out_9));
  _7_Segment_Display u_7_segment_display_8 (
    .g(n2t_to_7seg_driver_7_out_3), .f(n2t_to_7seg_driver_7_out_4), .a(n2t_to_7seg_driver_7_out_9),
    .b(n2t_to_7seg_driver_7_out_8), .e(n2t_to_7seg_driver_7_out_5), .d(n2t_to_7seg_driver_7_out_6),
    .c(n2t_to_7seg_driver_7_out_7), .dp(n2t_to_7seg_driver_7_out_2));
  _2t_to_7seg_driver u_2t_to_7seg_driver_6 (
    .in_1(n6t_sti_1_out_6x___jo1____10j[7:4]), .out_2(n2t_to_7seg_driver_6_out_2),
    .out_3(n2t_to_7seg_driver_6_out_3), .out_4(n2t_to_7seg_driver_6_out_4),
    .out_5(n2t_to_7seg_driver_6_out_5), .out_6(n2t_to_7seg_driver_6_out_6),
    .out_7(n2t_to_7seg_driver_6_out_7), .out_8(n2t_to_7seg_driver_6_out_8), .out_9(n2t_to_7seg_driver_6_out_9));
  _2t_to_7seg_driver u_2t_to_7seg_driver_7 (
    .in_1(n6t_sti_1_out_6x___jo1____10j[3:0]), .out_2(n2t_to_7seg_driver_7_out_2),
    .out_3(n2t_to_7seg_driver_7_out_3), .out_4(n2t_to_7seg_driver_7_out_4),
    .out_5(n2t_to_7seg_driver_7_out_5), .out_6(n2t_to_7seg_driver_7_out_6),
    .out_7(n2t_to_7seg_driver_7_out_7), .out_8(n2t_to_7seg_driver_7_out_8), .out_9(n2t_to_7seg_driver_7_out_9));
  _7_Segment_Display u_7_segment_display_9 (
    .g(n2t_to_7seg_driver_8_out_3), .f(n2t_to_7seg_driver_8_out_4), .a(n2t_to_7seg_driver_8_out_9),
    .b(n2t_to_7seg_driver_8_out_8), .e(n2t_to_7seg_driver_8_out_5), .d(n2t_to_7seg_driver_8_out_6),
    .c(n2t_to_7seg_driver_8_out_7), .dp(n2t_to_7seg_driver_8_out_2));
  _2t_to_7seg_driver u_2t_to_7seg_driver_8 (
    .in_1(keyboard_input_1_out_10[3:0]), .out_2(n2t_to_7seg_driver_8_out_2),
    .out_3(n2t_to_7seg_driver_8_out_3), .out_4(n2t_to_7seg_driver_8_out_4),
    .out_5(n2t_to_7seg_driver_8_out_5), .out_6(n2t_to_7seg_driver_8_out_6),
    .out_7(n2t_to_7seg_driver_8_out_7), .out_8(n2t_to_7seg_driver_8_out_8), .out_9(n2t_to_7seg_driver_8_out_9));
  _2t_to_7seg_driver u_2t_to_7seg_driver_9 (
    .in_1(keyboard_input_1_out_10[7:4]), .out_2(n2t_to_7seg_driver_9_out_2),
    .out_3(n2t_to_7seg_driver_9_out_3), .out_4(n2t_to_7seg_driver_9_out_4),
    .out_5(n2t_to_7seg_driver_9_out_5), .out_6(n2t_to_7seg_driver_9_out_6),
    .out_7(n2t_to_7seg_driver_9_out_7), .out_8(n2t_to_7seg_driver_9_out_8), .out_9(n2t_to_7seg_driver_9_out_9));
  LED led_13 (.in(tri_led_driver_6_out_2));
  LED led_14 (.in(tri_led_driver_5_out_2));
  LED led_15 (.in(tri_led_driver_7_out_2));
  LED led_16 (.in(tri_led_driver_6_out_3));
  tri_led_driver tri_led_driver_5 (
    .in_1(keyboard_input_1_out_10[3:2]), .out_2(tri_led_driver_5_out_2), .out_3(tri_led_driver_5_out_3),
    .out_4(tri_led_driver_5_out_4));
  LED led_17 (.in(tri_led_driver_5_out_3));
  tri_led_driver tri_led_driver_6 (
    .in_1(keyboard_input_1_out_10[5:4]), .out_2(tri_led_driver_6_out_2), .out_3(tri_led_driver_6_out_3),
    .out_4(tri_led_driver_6_out_4));
  LED led_18 (.in(tri_led_driver_5_out_4));
  LED led_19 (.in(tri_led_driver_7_out_4));
  LED led_20 (.in(tri_led_driver_6_out_4));
  Button Enter (.out(Enter_out));
  Button button (.out(button_out));
  Button neg (.out(neg_out));
  LED led_21 (.in(tri_led_driver_7_out_3));
  tri_led_driver tri_led_driver_7 (
    .in_1(keyboard_input_1_out_10[1:0]), .out_2(tri_led_driver_7_out_2), .out_3(tri_led_driver_7_out_3),
    .out_4(tri_led_driver_7_out_4));
  or or_1 (or_2_out[1], neg_out, 1'b0);
  or or_2 (or_2_out[0], button_out, 1'b0);
  // Probe on d_latch_level_triggered_1_q
  D_Latch__level_triggered d_latch_level_triggered_1 (
    .D(or_2_out), .E_1(pti_positive_trinary_inverter_1_jo1____11j), .Q(d_latch_level_triggered_1_q));
  buf or_3 (or_4_out[1], 1'b0);  // OR_Gate
  or or_4 (or_4_out[0], button_out, Enter_out, neg_out);
  _6t_3_1_MUX u_6t_3_1_mux_1 (
    .in_1(n6t_ripple_carry_adder_1_out_4), .in_2(keyboard_input_1_out_10),
    .in_3(n6t_sti_1_out_6x___jo1____10j), .in_4(d_latch_level_triggered_1_q), .out_5(n6t_3_1_mux_1_out_5));
  // Probe on d_latch_level_triggered_2_q
  D_Latch__level_triggered d_latch_level_triggered_2 (
    .D(or_4_out), .E_1(pti_positive_trinary_inverter_1_jo1____11j), .Q(d_latch_level_triggered_2_q));
  or or_5 (or_5_out[0], Enter_out, 1'b0);
  or or_6 (or_5_out[1], button_out, 1'b0);
  _6t_3_1_MUX u_6t_3_1_mux_2 (
    .in_1(n6t_3_1_mux_1_out_5), .in_2({n6t_register_1_q_2, n6t_register_1_q}), .in_3(n6t_register_2_q),
    .in_4(d_latch_level_triggered_2_q), .out_5(n6t_3_1_mux_2_out_5));
  _6t_3_1_MUX u_6t_3_1_mux_3 (
    .in_1({n6t_register_1_q_2, n6t_register_1_q}), .in_2(n6t_register_2_q),
    .in_3(n6t_x_18_stack_1_top_of_stack), .in_4(d_latch_level_triggered_3_q), .out_5(n6t_3_1_mux_3_out_5));
  // Probe on d_latch_level_triggered_3_q
  D_Latch__level_triggered d_latch_level_triggered_3 (
    .D(or_5_out), .E_1(pti_positive_trinary_inverter_1_jo1____11j), .Q(d_latch_level_triggered_3_q));
  or or_7 (or_8_out[1], button_out, 1'b0);
  or or_8 (or_8_out[0], Enter_out, 1'b0);
  _6t_x_18_stack u_6t_x_18_stack_1 (
    .j_pop__1_push__0_nop(d_latch_level_triggered_4_q), .in(n6t_register_2_q),
    .clock(cu_cycle_up_8_jo1____o1j), .top_of_stack(n6t_x_18_stack_1_top_of_stack));
  // Probe on cu_cycle_up_8_jo1____o1j
  // Probe on d_latch_level_triggered_4_q
  D_Latch__level_triggered d_latch_level_triggered_4 (
    .D(or_8_out), .E_1(pti_positive_trinary_inverter_1_jo1____11j), .Q(d_latch_level_triggered_4_q));
  PTI_Positive_Trinary_Inverter pti_positive_trinary_inverter_1 (
    .in_1(tor_max_3_input_1_out_4), .jo1____11j(pti_positive_trinary_inverter_1_jo1____11j));
  _6t_Register u_6t_register_1 (
    .D(n6t_3_1_mux_2_out_5), .clock(cu_cycle_up_8_jo1____o1j), .Q({n6t_register_1_q_2, n6t_register_1_q}));
  _6t_Register u_6t_register_2 (.D(n6t_3_1_mux_3_out_5), .clock(cu_cycle_up_8_jo1____o1j), .Q(n6t_register_2_q));
  TOR__max__3_input tor_max_3_input_1 (
    .in_1({1'b0, or_9_out[0]}), .in_2({1'b0, or_9_out[0]}), .in_3(cu_cycle_up_5_jo1____o1j),
    .out_4(tor_max_3_input_1_out_4));
  or or_9 (or_9_out[0], Enter_out, button_out, neg_out);
  _7_Segment_Display u_7_segment_display_10 (
    .g(n2t_to_7seg_driver_13_out_3), .f(n2t_to_7seg_driver_13_out_4), .a(n2t_to_7seg_driver_13_out_9),
    .b(n2t_to_7seg_driver_13_out_8), .e(n2t_to_7seg_driver_13_out_5), .d(n2t_to_7seg_driver_13_out_6),
    .c(n2t_to_7seg_driver_13_out_7), .dp(n2t_to_7seg_driver_13_out_2));
  _7_Segment_Display u_7_segment_display_11 (
    .g(n2t_to_7seg_driver_10_out_3), .f(n2t_to_7seg_driver_10_out_4), .a(n2t_to_7seg_driver_10_out_9),
    .b(n2t_to_7seg_driver_10_out_8), .e(n2t_to_7seg_driver_10_out_5), .d(n2t_to_7seg_driver_10_out_6),
    .c(n2t_to_7seg_driver_10_out_7), .dp(n2t_to_7seg_driver_10_out_2));
  _2t_to_7seg_driver u_2t_to_7seg_driver_10 (
    .in_1(n6t_register_1_q_2[11:8]), .out_2(n2t_to_7seg_driver_10_out_2),
    .out_3(n2t_to_7seg_driver_10_out_3), .out_4(n2t_to_7seg_driver_10_out_4),
    .out_5(n2t_to_7seg_driver_10_out_5), .out_6(n2t_to_7seg_driver_10_out_6),
    .out_7(n2t_to_7seg_driver_10_out_7), .out_8(n2t_to_7seg_driver_10_out_8),
    .out_9(n2t_to_7seg_driver_10_out_9));
  _7_Segment_Display u_7_segment_display_12 (
    .g(n2t_to_7seg_driver_14_out_3), .f(n2t_to_7seg_driver_14_out_4), .a(n2t_to_7seg_driver_14_out_9),
    .b(n2t_to_7seg_driver_14_out_8), .e(n2t_to_7seg_driver_14_out_5), .d(n2t_to_7seg_driver_14_out_6),
    .c(n2t_to_7seg_driver_14_out_7), .dp(n2t_to_7seg_driver_14_out_2));
  _7_Segment_Display u_7_segment_display_13 (
    .g(n2t_to_7seg_driver_11_out_3), .f(n2t_to_7seg_driver_11_out_4), .a(n2t_to_7seg_driver_11_out_9),
    .b(n2t_to_7seg_driver_11_out_8), .e(n2t_to_7seg_driver_11_out_5), .d(n2t_to_7seg_driver_11_out_6),
    .c(n2t_to_7seg_driver_11_out_7), .dp(n2t_to_7seg_driver_11_out_2));
  _2t_to_7seg_driver u_2t_to_7seg_driver_11 (
    .in_1(n6t_register_2_q[11:8]), .out_2(n2t_to_7seg_driver_11_out_2), .out_3(n2t_to_7seg_driver_11_out_3),
    .out_4(n2t_to_7seg_driver_11_out_4), .out_5(n2t_to_7seg_driver_11_out_5),
    .out_6(n2t_to_7seg_driver_11_out_6), .out_7(n2t_to_7seg_driver_11_out_7),
    .out_8(n2t_to_7seg_driver_11_out_8), .out_9(n2t_to_7seg_driver_11_out_9));
  _7_Segment_Display u_7_segment_display_14 (
    .g(n2t_to_7seg_driver_15_out_3), .f(n2t_to_7seg_driver_15_out_4), .a(n2t_to_7seg_driver_15_out_9),
    .b(n2t_to_7seg_driver_15_out_8), .e(n2t_to_7seg_driver_15_out_5), .d(n2t_to_7seg_driver_15_out_6),
    .c(n2t_to_7seg_driver_15_out_7), .dp(n2t_to_7seg_driver_15_out_2));
  _7_Segment_Display u_7_segment_display_15 (
    .g(n2t_to_7seg_driver_12_out_3), .f(n2t_to_7seg_driver_12_out_4), .a(n2t_to_7seg_driver_12_out_9),
    .b(n2t_to_7seg_driver_12_out_8), .e(n2t_to_7seg_driver_12_out_5), .d(n2t_to_7seg_driver_12_out_6),
    .c(n2t_to_7seg_driver_12_out_7), .dp(n2t_to_7seg_driver_12_out_2));
  _2t_to_7seg_driver u_2t_to_7seg_driver_12 (
    .in_1(n6t_x_18_stack_1_top_of_stack[11:8]), .out_2(n2t_to_7seg_driver_12_out_2),
    .out_3(n2t_to_7seg_driver_12_out_3), .out_4(n2t_to_7seg_driver_12_out_4),
    .out_5(n2t_to_7seg_driver_12_out_5), .out_6(n2t_to_7seg_driver_12_out_6),
    .out_7(n2t_to_7seg_driver_12_out_7), .out_8(n2t_to_7seg_driver_12_out_8),
    .out_9(n2t_to_7seg_driver_12_out_9));
  _7_Segment_Display u_7_segment_display_16 (
    .g(n2t_to_7seg_driver_16_out_3), .f(n2t_to_7seg_driver_16_out_4), .a(n2t_to_7seg_driver_16_out_9),
    .b(n2t_to_7seg_driver_16_out_8), .e(n2t_to_7seg_driver_16_out_5), .d(n2t_to_7seg_driver_16_out_6),
    .c(n2t_to_7seg_driver_16_out_7), .dp(n2t_to_7seg_driver_16_out_2));
  _2t_to_7seg_driver u_2t_to_7seg_driver_13 (
    .in_1(n6t_register_1_q_2[7:4]), .out_2(n2t_to_7seg_driver_13_out_2), .out_3(n2t_to_7seg_driver_13_out_3),
    .out_4(n2t_to_7seg_driver_13_out_4), .out_5(n2t_to_7seg_driver_13_out_5),
    .out_6(n2t_to_7seg_driver_13_out_6), .out_7(n2t_to_7seg_driver_13_out_7),
    .out_8(n2t_to_7seg_driver_13_out_8), .out_9(n2t_to_7seg_driver_13_out_9));
  _7_Segment_Display u_7_segment_display_17 (
    .g(n2t_to_7seg_driver_17_out_3), .f(n2t_to_7seg_driver_17_out_4), .a(n2t_to_7seg_driver_17_out_9),
    .b(n2t_to_7seg_driver_17_out_8), .e(n2t_to_7seg_driver_17_out_5), .d(n2t_to_7seg_driver_17_out_6),
    .c(n2t_to_7seg_driver_17_out_7), .dp(n2t_to_7seg_driver_17_out_2));
  _2t_to_7seg_driver u_2t_to_7seg_driver_14 (
    .in_1(n6t_register_2_q[7:4]), .out_2(n2t_to_7seg_driver_14_out_2), .out_3(n2t_to_7seg_driver_14_out_3),
    .out_4(n2t_to_7seg_driver_14_out_4), .out_5(n2t_to_7seg_driver_14_out_5),
    .out_6(n2t_to_7seg_driver_14_out_6), .out_7(n2t_to_7seg_driver_14_out_7),
    .out_8(n2t_to_7seg_driver_14_out_8), .out_9(n2t_to_7seg_driver_14_out_9));
  _7_Segment_Display u_7_segment_display_18 (
    .g(n2t_to_7seg_driver_18_out_3), .f(n2t_to_7seg_driver_18_out_4), .a(n2t_to_7seg_driver_18_out_9),
    .b(n2t_to_7seg_driver_18_out_8), .e(n2t_to_7seg_driver_18_out_5), .d(n2t_to_7seg_driver_18_out_6),
    .c(n2t_to_7seg_driver_18_out_7), .dp(n2t_to_7seg_driver_18_out_2));
  _2t_to_7seg_driver u_2t_to_7seg_driver_15 (
    .in_1(n6t_x_18_stack_1_top_of_stack[7:4]), .out_2(n2t_to_7seg_driver_15_out_2),
    .out_3(n2t_to_7seg_driver_15_out_3), .out_4(n2t_to_7seg_driver_15_out_4),
    .out_5(n2t_to_7seg_driver_15_out_5), .out_6(n2t_to_7seg_driver_15_out_6),
    .out_7(n2t_to_7seg_driver_15_out_7), .out_8(n2t_to_7seg_driver_15_out_8),
    .out_9(n2t_to_7seg_driver_15_out_9));
  CU_Cycle_Up cu_cycle_up_1 (.in_1(cu_cycle_up_8_jo1____o1j), .jo1____o1j(cu_cycle_up_1_jo1____o1j));
  CU_Cycle_Up cu_cycle_up_2 (.in_1(cu_cycle_up_1_jo1____o1j), .jo1____o1j(cu_cycle_up_2_jo1____o1j));
  CU_Cycle_Up cu_cycle_up_3 (.in_1({1'b0, or_9_out[0]}), .jo1____o1j(cu_cycle_up_3_jo1____o1j));
  CU_Cycle_Up cu_cycle_up_4 (.in_1(cu_cycle_up_3_jo1____o1j), .jo1____o1j(cu_cycle_up_4_jo1____o1j));
  _2t_to_7seg_driver u_2t_to_7seg_driver_16 (
    .in_1(n6t_register_1_q), .out_2(n2t_to_7seg_driver_16_out_2), .out_3(n2t_to_7seg_driver_16_out_3),
    .out_4(n2t_to_7seg_driver_16_out_4), .out_5(n2t_to_7seg_driver_16_out_5),
    .out_6(n2t_to_7seg_driver_16_out_6), .out_7(n2t_to_7seg_driver_16_out_7),
    .out_8(n2t_to_7seg_driver_16_out_8), .out_9(n2t_to_7seg_driver_16_out_9));
  _2t_to_7seg_driver u_2t_to_7seg_driver_17 (
    .in_1(n6t_register_2_q[3:0]), .out_2(n2t_to_7seg_driver_17_out_2), .out_3(n2t_to_7seg_driver_17_out_3),
    .out_4(n2t_to_7seg_driver_17_out_4), .out_5(n2t_to_7seg_driver_17_out_5),
    .out_6(n2t_to_7seg_driver_17_out_6), .out_7(n2t_to_7seg_driver_17_out_7),
    .out_8(n2t_to_7seg_driver_17_out_8), .out_9(n2t_to_7seg_driver_17_out_9));
  _2t_to_7seg_driver u_2t_to_7seg_driver_18 (
    .in_1(n6t_x_18_stack_1_top_of_stack[3:0]), .out_2(n2t_to_7seg_driver_18_out_2),
    .out_3(n2t_to_7seg_driver_18_out_3), .out_4(n2t_to_7seg_driver_18_out_4),
    .out_5(n2t_to_7seg_driver_18_out_5), .out_6(n2t_to_7seg_driver_18_out_6),
    .out_7(n2t_to_7seg_driver_18_out_7), .out_8(n2t_to_7seg_driver_18_out_8),
    .out_9(n2t_to_7seg_driver_18_out_9));
  CU_Cycle_Up cu_cycle_up_5 (.in_1(cu_cycle_up_2_jo1____o1j), .jo1____o1j(cu_cycle_up_5_jo1____o1j));
  CU_Cycle_Up cu_cycle_up_6 (.in_1(cu_cycle_up_5_jo1____o1j), .jo1____o1j(cu_cycle_up_6_jo1____o1j));
  CU_Cycle_Up cu_cycle_up_7 (.in_1(cu_cycle_up_8_jo1____o1j), .jo1____o1j(cu_cycle_up_7_jo1____o1j));
  CU_Cycle_Up cu_cycle_up_8 (.in_1(cu_cycle_up_4_jo1____o1j), .jo1____o1j(cu_cycle_up_8_jo1____o1j));
  CU_Cycle_Up cu_cycle_up_9 (.in_1(cu_cycle_up_6_jo1____o1j), .jo1____o1j(cu_cycle_up_9_jo1____o1j));
  CU_Cycle_Up cu_cycle_up_10 (.in_1(cu_cycle_up_7_jo1____o1j), .jo1____o1j(cu_cycle_up_10_jo1____o1j));
  CU_Cycle_Up cu_cycle_up_11 (.in_1(cu_cycle_up_9_jo1____o1j), .jo1____o1j(cu_cycle_up_11_jo1____o1j));
  CU_Cycle_Up cu_cycle_up_12 (.in_1(cu_cycle_up_10_jo1____o1j), .jo1____o1j(cu_cycle_up_12_jo1____o1j));
endmodule

module STI_Simple_Ternary_Inverter (
  input  [1:0] in_1,
  output [1:0] jo1____1oj
);


  assign jo1____1oj = {in_1[0], in_1[1]};

  // Notes on the sheet:
  //   Shocking?  Click the two split/joins the wires are crossed.
endmodule

module NTI_Negative_Trinary_Inverter (
  input  [1:0] in_1,
  output [1:0] jo1____1jj
);

  wire decoder_1_out0, decoder_1_out1, decoder_1_out3;

  Decoder #(.select(2)) decoder_1 (
    .out0(decoder_1_out0), .out1(decoder_1_out1), .out2(jo1____1jj[0]), .out3(decoder_1_out3), .sel(in_1));
  or or_1 (jo1____1jj[1], decoder_1_out0, decoder_1_out1, decoder_1_out3);
endmodule

module NTI_alternate__realistic__safe (
  input  [1:0] in_1,
  output [1:0] jo1____1jj
);

  wire not_1_out, not_2_out;

  not not_1 (not_1_out, in_1[0]);
  not not_2 (not_2_out, in_1[1]);
  and and_1 (jo1____1jj[0], in_1[1], not_1_out);
  or or_1 (jo1____1jj[1], in_1[0], not_2_out);

  // Notes on the sheet:
  //   In the simulator this may be slower, but IRL it is faster.
  //   This is about 2 gate delays, the other version using a decoder is about 3 gate delays.
endmodule

module PTI_Positive_Trinary_Inverter (
  input  [1:0] in_1,
  output [1:0] jo1____11j
);

  wire decoder_1_out0, decoder_1_out2, decoder_1_out3;

  Decoder #(.select(2)) decoder_1 (
    .out0(decoder_1_out0), .out1(jo1____11j[1]), .out2(decoder_1_out2), .out3(decoder_1_out3), .sel(in_1));
  or or_1 (jo1____11j[0], decoder_1_out0, decoder_1_out2, decoder_1_out3);
endmodule

module PTI_alternate__realistic__safe (
  input  [1:0] in_1,
  output [1:0] jo1____11j
);

  wire not_1_out, not_2_out;

  not not_1 (not_1_out, in_1[0]);
  not not_2 (not_2_out, in_1[1]);
  or or_1 (jo1____11j[0], in_1[1], not_1_out);
  and and_1 (jo1____11j[1], in_1[0], not_2_out);

  // Notes on the sheet:
  //   In the simulator this may be slower, but IRL it is faster.
  //   This is about 2 gate delays, the other version using a decoder is about 3 gate delays.
endmodule

module CU_Cycle_Up (
  input  [1:0] in_1,
  output [1:0] jo1____o1j
);

  wire decoder_1_out0, decoder_1_out2, decoder_1_out3;

  Decoder #(.select(2)) decoder_1 (
    .out0(decoder_1_out0), .out1(jo1____o1j[1]), .out2(decoder_1_out2), .out3(decoder_1_out3), .sel(in_1));
  or or_1 (jo1____o1j[0], decoder_1_out0, decoder_1_out3);
endmodule

module CD_Cycle_Down (
  input  [1:0] in_1,
  output [1:0] jo1____1jo
);

  wire decoder_1_out0, decoder_1_out1, decoder_1_out3;

  Decoder #(.select(2)) decoder_1 (
    .out0(decoder_1_out0), .out1(decoder_1_out1), .out2(jo1____1jo[0]), .out3(decoder_1_out3), .sel(in_1));
  or or_1 (jo1____1jo[1], decoder_1_out0, decoder_1_out3);
endmodule

module TNAND_3_input (
  input  [1:0] in_1,
  input  [1:0] in_2,
  input  [1:0] in_3,
  output [1:0] out_4
);

  wire decoder_1_out0, decoder_1_out1, decoder_1_out2, decoder_1_out3, decoder_2_out0, decoder_2_out1,
       decoder_2_out2, decoder_2_out3, decoder_3_out0, decoder_3_out1, decoder_3_out2, decoder_3_out3;

  Decoder #(.select(2)) decoder_1 (
    .out0(decoder_1_out0), .out1(decoder_1_out1), .out2(decoder_1_out2), .out3(decoder_1_out3), .sel(in_1));
  Decoder #(.select(2)) decoder_2 (
    .out0(decoder_2_out0), .out1(decoder_2_out1), .out2(decoder_2_out2), .out3(decoder_2_out3), .sel(in_2));
  Decoder #(.select(2)) decoder_3 (
    .out0(decoder_3_out0), .out1(decoder_3_out1), .out2(decoder_3_out2), .out3(decoder_3_out3), .sel(in_3));
  and and_1 (out_4[1], decoder_1_out1, decoder_2_out1, decoder_3_out1);
  or or_1 (out_4[0], decoder_1_out2, decoder_2_out2, decoder_3_out2);

  // Notes on the sheet:
  //   Treat 11 as 00
  //   Decoders aren't required,
  //   But they make the circuit
  //   If all inputs are 1, TNAND is -1
  //   If any input is -1, TNAND is 1
  //   Otherwise, TNAND is 0
endmodule

module TNAND_fast__3_input__unsafe (
  input  [1:0] in_1,
  input  [1:0] in_2,
  input  [1:0] in_3,
  output [1:0] out_4
);

  and and_1 (out_4[1], in_3[0], in_2[0], in_1[0]);
  or or_1 (out_4[0], in_1[1], in_2[1], in_3[1]);

  // Notes on the sheet:
  //   See notes on TNAND fast, 2 input
  //   If all inputs are 1, TNAND is -1
  //   If any input is -1, TNAND is 1
  //   Otherwise, TNAND is 0
endmodule

module TNAND_fast__2_input__unsafe (
  input  [1:0] in_1,
  input  [1:0] in_2,
  output [1:0] out_3
);

  and and_1 (out_3[1], in_1[0], in_2[0]);
  or or_1 (out_3[0], in_1[1], in_2[1]);

  // Notes on the sheet:
  //   This circuit will simulate faster.  It is unsafe in the sense that
  //   It treats 11 input as *both* 1 and -1, and generates bad output
  //   To see the bug, try the inputs 00 and 11.
  //   The result should be 00 in both cases.  But for 11 it is 01.
  //   This is probably the right way to implement all the gates, and if I did
  //   this in real hardware I probably would.  But I'm lazy, and having the
  //   the decoders around turning 11 into 00 is safer, hides bugs.
  //   If all inputs are 1, TNAND is -1
  //   If any input is -1, TNAND is 1
  //   Otherwise, TNAND is 0
endmodule

module TNOR_3_input (
  input  [1:0] in_1,
  input  [1:0] in_2,
  input  [1:0] in_3,
  output [1:0] out_4
);

  wire decoder_1_out0, decoder_1_out1, decoder_1_out2, decoder_1_out3, decoder_2_out0, decoder_2_out1,
       decoder_2_out2, decoder_2_out3, decoder_3_out0, decoder_3_out1, decoder_3_out2, decoder_3_out3;

  Decoder #(.select(2)) decoder_1 (
    .out0(decoder_1_out0), .out1(decoder_1_out1), .out2(decoder_1_out2), .out3(decoder_1_out3), .sel(in_1));
  Decoder #(.select(2)) decoder_2 (
    .out0(decoder_2_out0), .out1(decoder_2_out1), .out2(decoder_2_out2), .out3(decoder_2_out3), .sel(in_2));
  Decoder #(.select(2)) decoder_3 (
    .out0(decoder_3_out0), .out1(decoder_3_out1), .out2(decoder_3_out2), .out3(decoder_3_out3), .sel(in_3));
  or or_1 (out_4[1], decoder_1_out1, decoder_2_out1, decoder_3_out1);
  and and_1 (out_4[0], decoder_1_out2, decoder_2_out2, decoder_3_out2);

  // Notes on the sheet:
  //   Treat 11 as 00
  //   Decoders aren't required,
  //   But they make the circuit
  //   If any input is 1, TNOR is -1
  //   If all inputs are -1, TNOR is 1
  //   Otherwise, TNOR is 0
endmodule

module TNOR_fast__2_input__unsafe (
  input  [1:0] in_1,
  input  [1:0] in_2,
  output [1:0] out_3
);

  and and_1 (out_3[0], in_1[1], in_2[1]);
  or or_1 (out_3[1], in_2[0], in_1[0]);

  // Notes on the sheet:
  //   See note on TNAND fast
  //   If all inputs are -1, TNOR is 1
  //   If any input is 1, TNOR is -1
  //   Otherwise, TNOR is 0
endmodule

module TAND__min__3_input (
  input  [1:0] in_1,
  input  [1:0] in_2,
  input  [1:0] in_3,
  output [1:0] out_4
);

  wire decoder_1_out0, decoder_1_out1, decoder_1_out2, decoder_1_out3, decoder_2_out0, decoder_2_out1,
       decoder_2_out2, decoder_2_out3, decoder_3_out0, decoder_3_out1, decoder_3_out2, decoder_3_out3;

  Decoder #(.select(2)) decoder_1 (
    .out0(decoder_1_out0), .out1(decoder_1_out1), .out2(decoder_1_out2), .out3(decoder_1_out3), .sel(in_1));
  Decoder #(.select(2)) decoder_2 (
    .out0(decoder_2_out0), .out1(decoder_2_out1), .out2(decoder_2_out2), .out3(decoder_2_out3), .sel(in_2));
  Decoder #(.select(2)) decoder_3 (
    .out0(decoder_3_out0), .out1(decoder_3_out1), .out2(decoder_3_out2), .out3(decoder_3_out3), .sel(in_3));
  and and_1 (out_4[0], decoder_1_out1, decoder_2_out1, decoder_3_out1);
  or or_1 (out_4[1], decoder_1_out2, decoder_2_out2, decoder_3_out2);

  // Notes on the sheet:
  //   Treat 11 as 00
  //   Decoders aren't required,
  //   But they make the circuit
  //   If all inputs are 1, min is 1
  //   If any input is -1, min is -1
  //   Otherwise, min is 0
endmodule

module TAND_fast__2_input__unsafe (
  input  [1:0] in_1,
  input  [1:0] in_2,
  output [1:0] out_3
);

  and and_1 (out_3[0], in_1[0], in_2[0]);
  or or_1 (out_3[1], in_1[1], in_2[1]);

  // Notes on the sheet:
  //   See the notes on TNAND fast
  //   If all inputs are 1, min is 1
  //   If any input is -1, min is -1
  //   Otherwise, min is 0
endmodule

module TOR__max__3_input (
  input  [1:0] in_1,
  input  [1:0] in_2,
  input  [1:0] in_3,
  output [1:0] out_4
);

  wire decoder_1_out0, decoder_1_out1, decoder_1_out2, decoder_1_out3, decoder_2_out0, decoder_2_out1,
       decoder_2_out2, decoder_2_out3, decoder_3_out0, decoder_3_out1, decoder_3_out2, decoder_3_out3;

  Decoder #(.select(2)) decoder_1 (
    .out0(decoder_1_out0), .out1(decoder_1_out1), .out2(decoder_1_out2), .out3(decoder_1_out3), .sel(in_1));
  Decoder #(.select(2)) decoder_2 (
    .out0(decoder_2_out0), .out1(decoder_2_out1), .out2(decoder_2_out2), .out3(decoder_2_out3), .sel(in_2));
  Decoder #(.select(2)) decoder_3 (
    .out0(decoder_3_out0), .out1(decoder_3_out1), .out2(decoder_3_out2), .out3(decoder_3_out3), .sel(in_3));
  or or_1 (out_4[0], decoder_1_out1, decoder_2_out1, decoder_3_out1);
  and and_1 (out_4[1], decoder_1_out2, decoder_2_out2, decoder_3_out2);

  // Notes on the sheet:
  //   Treat 11 as 00
  //   Decoders aren't required,
  //   But they make the circuit
  //   If any input is 1, max is 1
  //   If all inputs are -1, max is -1
  //   Otherwise, max is 0
endmodule

module TOR_fast__2_input__unsafe (
  input  [1:0] in_1,
  input  [1:0] in_2,
  output [1:0] out_3
);

  or or_1 (out_3[0], in_1[0], in_2[0]);
  and and_1 (out_3[1], in_2[1], in_1[1]);

  // Notes on the sheet:
  //   See note on TNAND fast
  //   If any input is 1, TOR is 1
  //   If all inputs are -1, TOR is -1
  //   Otherwise, TNOR is 0
endmodule

module _1_Constant_Trit (
  output [1:0] _1_constant
);


  assign _1_constant = 2'b01;
endmodule

module _0_Constant_Trit (
  output [1:0] _0_constant
);


  assign _0_constant = 2'b00;

  // Notes on the sheet:
  //   0
endmodule

module _1_Constant_Trit_2 (
  output [1:0] minus_1_constant
);


  assign minus_1_constant = 2'b10;
endmodule

module _1_3_decoder (
  input  [1:0] S,
  output [1:0] if__S__1__j_else_1,
  output [1:0] if__S__0__j_else_1,
  output [1:0] if__S__j__j_else_1
);

  wire [1:0] pti_alternate_realistic_safe_1_jo1____11j;

  PTI_alternate__realistic__safe pti_alternate_realistic_safe_1 (
    .in_1(S), .jo1____11j(pti_alternate_realistic_safe_1_jo1____11j));
  NTI_alternate__realistic__safe nti_alternate_realistic_safe_1 (.in_1(S), .jo1____1jj(if__S__j__j_else_1));
  STI_Simple_Ternary_Inverter sti_simple_ternary_inverter_1 (
    .in_1(pti_alternate_realistic_safe_1_jo1____11j), .jo1____1oj(if__S__1__j_else_1));
  TNOR_fast__2_input__unsafe tnor_fast_2_input_unsafe_1 (
    .in_1(if__S__1__j_else_1), .in_2(if__S__j__j_else_1), .out_3(if__S__0__j_else_1));

  // Notes on the sheet:
  //   See 3:1 MUX to see one way to use outputs
endmodule

module _3_1_3_control_mux_body (
  input  [1:0] In1,
  input  [1:0] In0,
  input  [1:0] Inj,
  input  [1:0] Sel1_j,
  input  [1:0] Sel0_j,
  input  [1:0] Selj_j,
  output [1:0] \output 
);

  wire [1:0] tnand_fast_2_input_unsafe_1_out_3, tnand_fast_2_input_unsafe_2_out_3,
       tnand_fast_2_input_unsafe_3_out_3;

  TNAND_fast__2_input__unsafe tnand_fast_2_input_unsafe_1 (
    .in_1(In1), .in_2(Sel1_j), .out_3(tnand_fast_2_input_unsafe_1_out_3));
  TNAND_fast__2_input__unsafe tnand_fast_2_input_unsafe_2 (
    .in_1(In0), .in_2(Sel0_j), .out_3(tnand_fast_2_input_unsafe_2_out_3));
  TNAND_fast__2_input__unsafe tnand_fast_2_input_unsafe_3 (
    .in_1(Inj), .in_2(Selj_j), .out_3(tnand_fast_2_input_unsafe_3_out_3));
  TNAND_fast__3_input__unsafe tnand_fast_3_input_unsafe_1 (
    .in_1(tnand_fast_2_input_unsafe_1_out_3), .in_2(tnand_fast_2_input_unsafe_2_out_3),
    .in_3(tnand_fast_2_input_unsafe_3_out_3), .out_4(\output ));
endmodule

module _3_1_MUX (
  input  [1:0] In1,
  input  [1:0] In0,
  input  [1:0] Inj,
  input  [1:0] select,
  output [1:0] \output 
);

  wire [1:0] nti_alternate_realistic_safe_1_jo1____1jj, pti_alternate_realistic_safe_1_jo1____11j,
       sti_simple_ternary_inverter_1_jo1____1oj, tnand_fast_2_input_unsafe_1_out_3,
       tnand_fast_2_input_unsafe_2_out_3, tnand_fast_2_input_unsafe_3_out_3, tnor_fast_2_input_unsafe_1_out_3;

  STI_Simple_Ternary_Inverter sti_simple_ternary_inverter_1 (
    .in_1(pti_alternate_realistic_safe_1_jo1____11j), .jo1____1oj(sti_simple_ternary_inverter_1_jo1____1oj));
  PTI_alternate__realistic__safe pti_alternate_realistic_safe_1 (
    .in_1(select), .jo1____11j(pti_alternate_realistic_safe_1_jo1____11j));
  TNOR_fast__2_input__unsafe tnor_fast_2_input_unsafe_1 (
    .in_1(sti_simple_ternary_inverter_1_jo1____1oj), .in_2(nti_alternate_realistic_safe_1_jo1____1jj),
    .out_3(tnor_fast_2_input_unsafe_1_out_3));
  NTI_alternate__realistic__safe nti_alternate_realistic_safe_1 (
    .in_1(select), .jo1____1jj(nti_alternate_realistic_safe_1_jo1____1jj));
  TNAND_fast__2_input__unsafe tnand_fast_2_input_unsafe_1 (
    .in_1(In1), .in_2(sti_simple_ternary_inverter_1_jo1____1oj), .out_3(tnand_fast_2_input_unsafe_1_out_3));
  TNAND_fast__2_input__unsafe tnand_fast_2_input_unsafe_2 (
    .in_1(In0), .in_2(tnor_fast_2_input_unsafe_1_out_3), .out_3(tnand_fast_2_input_unsafe_2_out_3));
  TNAND_fast__2_input__unsafe tnand_fast_2_input_unsafe_3 (
    .in_1(Inj), .in_2(nti_alternate_realistic_safe_1_jo1____1jj), .out_3(tnand_fast_2_input_unsafe_3_out_3));
  TNAND_fast__3_input__unsafe tnand_fast_3_input_unsafe_1 (
    .in_1(tnand_fast_2_input_unsafe_1_out_3), .in_2(tnand_fast_2_input_unsafe_2_out_3),
    .in_3(tnand_fast_2_input_unsafe_3_out_3), .out_4(\output ));
endmodule

module D_Latch__level_triggered (
  input  [1:0] D,
  input  [1:0] E_1,
  output [1:0] Q
);

  wire [1:0] pti_positive_trinary_inverter_1_jo1____11j, sti_simple_ternary_inverter_1_jo1____1oj,
       tnand_3_input_1_out_4, tnand_fast_2_input_unsafe_1_out_3;

  PTI_Positive_Trinary_Inverter pti_positive_trinary_inverter_1 (
    .in_1(E_1), .jo1____11j(pti_positive_trinary_inverter_1_jo1____11j));
  STI_Simple_Ternary_Inverter sti_simple_ternary_inverter_1 (
    .in_1(pti_positive_trinary_inverter_1_jo1____11j), .jo1____1oj(sti_simple_ternary_inverter_1_jo1____1oj));
  TNAND_3_input tnand_3_input_1 (
    .in_1(D), .in_2(D), .in_3(sti_simple_ternary_inverter_1_jo1____1oj), .out_4(tnand_3_input_1_out_4));
  TNAND_fast__2_input__unsafe tnand_fast_2_input_unsafe_1 (
    .in_1(pti_positive_trinary_inverter_1_jo1____11j), .in_2(Q), .out_3(tnand_fast_2_input_unsafe_1_out_3));
  TNAND_fast__2_input__unsafe tnand_fast_2_input_unsafe_2 (
    .in_1(tnand_3_input_1_out_4), .in_2(tnand_fast_2_input_unsafe_1_out_3), .out_3(Q));
endmodule

module Register__master_slave_D_latch (
  input  [1:0] D,
  input  [1:0] Clock__pulse__latch_in_on_rising_edge__out_on_falling,
  output [1:0] Q
);

  wire [1:0] d_latch_level_triggered_1_q, pti_positive_trinary_inverter_1_jo1____11j,
       sti_simple_ternary_inverter_1_jo1____1oj;

  STI_Simple_Ternary_Inverter sti_simple_ternary_inverter_1 (
    .in_1(pti_positive_trinary_inverter_1_jo1____11j), .jo1____1oj(sti_simple_ternary_inverter_1_jo1____1oj));
  D_Latch__level_triggered d_latch_level_triggered_1 (
    .D(D), .E_1(sti_simple_ternary_inverter_1_jo1____1oj), .Q(d_latch_level_triggered_1_q));
  PTI_Positive_Trinary_Inverter pti_positive_trinary_inverter_1 (
    .in_1(Clock__pulse__latch_in_on_rising_edge__out_on_falling),
    .jo1____11j(pti_positive_trinary_inverter_1_jo1____11j));
  D_Latch__level_triggered d_latch_level_triggered_2 (
    .D(d_latch_level_triggered_1_q), .E_1(pti_positive_trinary_inverter_1_jo1____11j), .Q(Q));
endmodule

module D_Latch_w_Async_Reset (
  input  [1:0] D,
  input  [1:0] E_1,
  input  [1:0] Reset__Q__1_when_Reset_1__async,
  output [1:0] Q
);

  wire [1:0] pti_positive_trinary_inverter_1_jo1____11j, pti_positive_trinary_inverter_2_jo1____11j,
       sti_simple_ternary_inverter_1_jo1____1oj, tnand_fast_3_input_unsafe_1_out_4,
       tnand_fast_3_input_unsafe_2_out_4;

  PTI_Positive_Trinary_Inverter pti_positive_trinary_inverter_1 (
    .in_1(E_1), .jo1____11j(pti_positive_trinary_inverter_1_jo1____11j));
  PTI_Positive_Trinary_Inverter pti_positive_trinary_inverter_2 (
    .in_1(Reset__Q__1_when_Reset_1__async), .jo1____11j(pti_positive_trinary_inverter_2_jo1____11j));
  STI_Simple_Ternary_Inverter sti_simple_ternary_inverter_1 (
    .in_1(pti_positive_trinary_inverter_1_jo1____11j), .jo1____1oj(sti_simple_ternary_inverter_1_jo1____1oj));
  TNAND_fast__3_input__unsafe tnand_fast_3_input_unsafe_1 (
    .in_1(D), .in_2(pti_positive_trinary_inverter_2_jo1____11j),
    .in_3(sti_simple_ternary_inverter_1_jo1____1oj), .out_4(tnand_fast_3_input_unsafe_1_out_4));
  TNAND_fast__3_input__unsafe tnand_fast_3_input_unsafe_2 (
    .in_1(pti_positive_trinary_inverter_1_jo1____11j), .in_2(pti_positive_trinary_inverter_2_jo1____11j),
    .in_3(Q), .out_4(tnand_fast_3_input_unsafe_2_out_4));
  TNAND_fast__2_input__unsafe tnand_fast_2_input_unsafe_1 (
    .in_1(tnand_fast_3_input_unsafe_1_out_4), .in_2(tnand_fast_3_input_unsafe_2_out_4), .out_3(Q));
endmodule

module Register_w_Async_Reset__master_slave_D_latch (
  input  [1:0] D,
  input  [1:0] Clock__pulse__latch_in_on_rising_edge__out_on_falling,
  input  [1:0] Reset__Q__1_when_Reset_1__async,
  output [1:0] Q
);

  wire [1:0] d_latch_w_async_reset_1_q, pti_positive_trinary_inverter_1_jo1____11j,
       sti_simple_ternary_inverter_1_jo1____1oj;

  STI_Simple_Ternary_Inverter sti_simple_ternary_inverter_1 (
    .in_1(pti_positive_trinary_inverter_1_jo1____11j), .jo1____1oj(sti_simple_ternary_inverter_1_jo1____1oj));
  D_Latch_w_Async_Reset d_latch_w_async_reset_1 (
    .D(D), .E_1(sti_simple_ternary_inverter_1_jo1____1oj),
    .Reset__Q__1_when_Reset_1__async(Reset__Q__1_when_Reset_1__async), .Q(d_latch_w_async_reset_1_q));
  PTI_Positive_Trinary_Inverter pti_positive_trinary_inverter_1 (
    .in_1(Clock__pulse__latch_in_on_rising_edge__out_on_falling),
    .jo1____11j(pti_positive_trinary_inverter_1_jo1____11j));
  D_Latch_w_Async_Reset d_latch_w_async_reset_2 (
    .D(d_latch_w_async_reset_1_q), .E_1(pti_positive_trinary_inverter_1_jo1____11j),
    .Reset__Q__1_when_Reset_1__async(Reset__Q__1_when_Reset_1__async), .Q(Q));
endmodule

module _1t_full_adder__lower_gate_count (
  input  [1:0] A,
  input  [1:0] B,
  input  [1:0] C,
  output [1:0] Carry_out,
  output [1:0] Sum_out
);

  wire [1:0] n1_3_decoder_1_if__s__0__j_else_1, n1_3_decoder_1_if__s__1__j_else_1,
       n1_3_decoder_1_if__s__j__j_else_1, n1_3_decoder_2_if__s__0__j_else_1,
       n1_3_decoder_2_if__s__1__j_else_1, n1_3_decoder_2_if__s__j__j_else_1,
       n1_3_decoder_3_if__s__0__j_else_1, n1_3_decoder_3_if__s__1__j_else_1,
       n1_3_decoder_3_if__s__j__j_else_1, n3_1_3_control_mux_body_1_output, n3_1_3_control_mux_body_2_output,
       n3_1_3_control_mux_body_3_output, n3_1_3_control_mux_body_4_output, n3_1_3_control_mux_body_6_output,
       n3_1_3_control_mux_body_7_output, n3_1_3_control_mux_body_8_output, n3_1_3_control_mux_body_9_output,
       n3_1_3_control_mux_body_10_output, n3_1_3_control_mux_body_12_output,
       n3_1_3_control_mux_body_13_output, n3_1_3_control_mux_body_14_output;

  _1_3_decoder u_1_3_decoder_1 (
    .S(A), .if__S__1__j_else_1(n1_3_decoder_1_if__s__1__j_else_1),
    .if__S__0__j_else_1(n1_3_decoder_1_if__s__0__j_else_1),
    .if__S__j__j_else_1(n1_3_decoder_1_if__s__j__j_else_1));
  _1_3_decoder u_1_3_decoder_2 (
    .S(B), .if__S__1__j_else_1(n1_3_decoder_2_if__s__1__j_else_1),
    .if__S__0__j_else_1(n1_3_decoder_2_if__s__0__j_else_1),
    .if__S__j__j_else_1(n1_3_decoder_2_if__s__j__j_else_1));
  _1_3_decoder u_1_3_decoder_3 (
    .S(C), .if__S__1__j_else_1(n1_3_decoder_3_if__s__1__j_else_1),
    .if__S__0__j_else_1(n1_3_decoder_3_if__s__0__j_else_1),
    .if__S__j__j_else_1(n1_3_decoder_3_if__s__j__j_else_1));
  _3_1_3_control_mux_body u_3_1_3_control_mux_body_1 (
    .In1(2'b10), .In0(2'b01), .Inj(2'b00), .Sel1_j(n1_3_decoder_1_if__s__1__j_else_1),
    .Sel0_j(n1_3_decoder_1_if__s__0__j_else_1), .Selj_j(n1_3_decoder_1_if__s__j__j_else_1),
    .\output (n3_1_3_control_mux_body_1_output));
  _3_1_3_control_mux_body u_3_1_3_control_mux_body_2 (
    .In1(A), .In0(n3_1_3_control_mux_body_3_output), .Inj(n3_1_3_control_mux_body_1_output),
    .Sel1_j(n1_3_decoder_2_if__s__1__j_else_1), .Sel0_j(n1_3_decoder_2_if__s__0__j_else_1),
    .Selj_j(n1_3_decoder_2_if__s__j__j_else_1), .\output (n3_1_3_control_mux_body_2_output));
  _3_1_3_control_mux_body u_3_1_3_control_mux_body_3 (
    .In1(2'b00), .In0(2'b10), .Inj(2'b01), .Sel1_j(n1_3_decoder_1_if__s__1__j_else_1),
    .Sel0_j(n1_3_decoder_1_if__s__0__j_else_1), .Selj_j(n1_3_decoder_1_if__s__j__j_else_1),
    .\output (n3_1_3_control_mux_body_3_output));
  _3_1_3_control_mux_body u_3_1_3_control_mux_body_4 (
    .In1(n3_1_3_control_mux_body_1_output), .In0(A), .Inj(n3_1_3_control_mux_body_3_output),
    .Sel1_j(n1_3_decoder_2_if__s__1__j_else_1), .Sel0_j(n1_3_decoder_2_if__s__0__j_else_1),
    .Selj_j(n1_3_decoder_2_if__s__j__j_else_1), .\output (n3_1_3_control_mux_body_4_output));
  _3_1_3_control_mux_body u_3_1_3_control_mux_body_5 (
    .In1(n3_1_3_control_mux_body_6_output), .In0(n3_1_3_control_mux_body_4_output),
    .Inj(n3_1_3_control_mux_body_2_output), .Sel1_j(n1_3_decoder_3_if__s__1__j_else_1),
    .Sel0_j(n1_3_decoder_3_if__s__0__j_else_1), .Selj_j(n1_3_decoder_3_if__s__j__j_else_1), .\output (Sum_out));
  _3_1_3_control_mux_body u_3_1_3_control_mux_body_6 (
    .In1(n3_1_3_control_mux_body_3_output), .In0(n3_1_3_control_mux_body_1_output), .Inj(A),
    .Sel1_j(n1_3_decoder_2_if__s__1__j_else_1), .Sel0_j(n1_3_decoder_2_if__s__0__j_else_1),
    .Selj_j(n1_3_decoder_2_if__s__j__j_else_1), .\output (n3_1_3_control_mux_body_6_output));
  _3_1_3_control_mux_body u_3_1_3_control_mux_body_7 (
    .In1(2'b00), .In0(2'b10), .Inj(2'b10), .Sel1_j(n1_3_decoder_1_if__s__1__j_else_1),
    .Sel0_j(n1_3_decoder_1_if__s__0__j_else_1), .Selj_j(n1_3_decoder_1_if__s__j__j_else_1),
    .\output (n3_1_3_control_mux_body_7_output));
  _3_1_3_control_mux_body u_3_1_3_control_mux_body_8 (
    .In1(2'b00), .In0(n3_1_3_control_mux_body_9_output), .Inj(n3_1_3_control_mux_body_7_output),
    .Sel1_j(n1_3_decoder_2_if__s__1__j_else_1), .Sel0_j(n1_3_decoder_2_if__s__0__j_else_1),
    .Selj_j(n1_3_decoder_2_if__s__j__j_else_1), .\output (n3_1_3_control_mux_body_8_output));
  _3_1_3_control_mux_body u_3_1_3_control_mux_body_9 (
    .In1(2'b00), .In0(2'b00), .Inj(2'b10), .Sel1_j(n1_3_decoder_1_if__s__1__j_else_1),
    .Sel0_j(n1_3_decoder_1_if__s__0__j_else_1), .Selj_j(n1_3_decoder_1_if__s__j__j_else_1),
    .\output (n3_1_3_control_mux_body_9_output));
  _3_1_3_control_mux_body u_3_1_3_control_mux_body_10 (
    .In1(n3_1_3_control_mux_body_12_output), .In0(2'b00), .Inj(n3_1_3_control_mux_body_9_output),
    .Sel1_j(n1_3_decoder_2_if__s__1__j_else_1), .Sel0_j(n1_3_decoder_2_if__s__0__j_else_1),
    .Selj_j(n1_3_decoder_2_if__s__j__j_else_1), .\output (n3_1_3_control_mux_body_10_output));
  _3_1_3_control_mux_body u_3_1_3_control_mux_body_11 (
    .In1(n3_1_3_control_mux_body_13_output), .In0(n3_1_3_control_mux_body_10_output),
    .Inj(n3_1_3_control_mux_body_8_output), .Sel1_j(n1_3_decoder_3_if__s__1__j_else_1),
    .Sel0_j(n1_3_decoder_3_if__s__0__j_else_1), .Selj_j(n1_3_decoder_3_if__s__j__j_else_1),
    .\output (Carry_out));
  _3_1_3_control_mux_body u_3_1_3_control_mux_body_12 (
    .In1(2'b01), .In0(2'b00), .Inj(2'b00), .Sel1_j(n1_3_decoder_1_if__s__1__j_else_1),
    .Sel0_j(n1_3_decoder_1_if__s__0__j_else_1), .Selj_j(n1_3_decoder_1_if__s__j__j_else_1),
    .\output (n3_1_3_control_mux_body_12_output));
  _3_1_3_control_mux_body u_3_1_3_control_mux_body_13 (
    .In1(n3_1_3_control_mux_body_14_output), .In0(n3_1_3_control_mux_body_12_output), .Inj(2'b00),
    .Sel1_j(n1_3_decoder_2_if__s__1__j_else_1), .Sel0_j(n1_3_decoder_2_if__s__0__j_else_1),
    .Selj_j(n1_3_decoder_2_if__s__j__j_else_1), .\output (n3_1_3_control_mux_body_13_output));
  _3_1_3_control_mux_body u_3_1_3_control_mux_body_14 (
    .In1(2'b01), .In0(2'b01), .Inj(2'b00), .Sel1_j(n1_3_decoder_1_if__s__1__j_else_1),
    .Sel0_j(n1_3_decoder_1_if__s__0__j_else_1), .Selj_j(n1_3_decoder_1_if__s__j__j_else_1),
    .\output (n3_1_3_control_mux_body_14_output));

  // Notes on the sheet:
  //   -1
  //   0
  //   1
endmodule

module _1t_full_adder (
  input  [1:0] A,
  input  [1:0] B,
  input  [1:0] C,
  output [1:0] Carry_out,
  output [1:0] Sum_out
);

  wire [1:0] n3_1_mux_1_output, n3_1_mux_2_output, n3_1_mux_3_output, n3_1_mux_4_output, n3_1_mux_6_output,
       n3_1_mux_7_output, n3_1_mux_8_output, n3_1_mux_9_output, n3_1_mux_10_output, n3_1_mux_12_output,
       n3_1_mux_13_output, n3_1_mux_14_output;

  _3_1_MUX u_3_1_mux_1 (.In1(2'b10), .In0(2'b01), .Inj(2'b00), .select(A), .\output (n3_1_mux_1_output));
  _3_1_MUX u_3_1_mux_2 (
    .In1(A), .In0(n3_1_mux_3_output), .Inj(n3_1_mux_1_output), .select(B), .\output (n3_1_mux_2_output));
  _3_1_MUX u_3_1_mux_3 (.In1(2'b00), .In0(2'b10), .Inj(2'b01), .select(A), .\output (n3_1_mux_3_output));
  _3_1_MUX u_3_1_mux_4 (
    .In1(n3_1_mux_1_output), .In0(A), .Inj(n3_1_mux_3_output), .select(B), .\output (n3_1_mux_4_output));
  _3_1_MUX u_3_1_mux_5 (
    .In1(n3_1_mux_6_output), .In0(n3_1_mux_4_output), .Inj(n3_1_mux_2_output), .select(C), .\output (Sum_out));
  _3_1_MUX u_3_1_mux_6 (
    .In1(n3_1_mux_3_output), .In0(n3_1_mux_1_output), .Inj(A), .select(B), .\output (n3_1_mux_6_output));
  _3_1_MUX u_3_1_mux_7 (.In1(2'b00), .In0(2'b10), .Inj(2'b10), .select(A), .\output (n3_1_mux_7_output));
  _3_1_MUX u_3_1_mux_8 (
    .In1(2'b00), .In0(n3_1_mux_9_output), .Inj(n3_1_mux_7_output), .select(B), .\output (n3_1_mux_8_output));
  _3_1_MUX u_3_1_mux_9 (.In1(2'b00), .In0(2'b00), .Inj(2'b10), .select(A), .\output (n3_1_mux_9_output));
  _3_1_MUX u_3_1_mux_10 (
    .In1(n3_1_mux_12_output), .In0(2'b00), .Inj(n3_1_mux_9_output), .select(B), .\output (n3_1_mux_10_output));
  _3_1_MUX u_3_1_mux_11 (
    .In1(n3_1_mux_13_output), .In0(n3_1_mux_10_output), .Inj(n3_1_mux_8_output), .select(C),
    .\output (Carry_out));
  _3_1_MUX u_3_1_mux_12 (.In1(2'b01), .In0(2'b00), .Inj(2'b00), .select(A), .\output (n3_1_mux_12_output));
  _3_1_MUX u_3_1_mux_13 (
    .In1(n3_1_mux_14_output), .In0(n3_1_mux_12_output), .Inj(2'b00), .select(B), .\output (n3_1_mux_13_output));
  _3_1_MUX u_3_1_mux_14 (.In1(2'b01), .In0(2'b01), .Inj(2'b00), .select(A), .\output (n3_1_mux_14_output));

  // Notes on the sheet:
  //   -1
  //   0
  //   1
endmodule

module _6t_STI (
  input  [11:0] in,
  output [11:0] out_6x___jo1____10j
);

  STI_Simple_Ternary_Inverter sti_simple_ternary_inverter_1 (.in_1(in[11:10]), .jo1____1oj(out_6x___jo1____10j[11:10]));
  STI_Simple_Ternary_Inverter sti_simple_ternary_inverter_2 (.in_1(in[9:8]), .jo1____1oj(out_6x___jo1____10j[9:8]));
  STI_Simple_Ternary_Inverter sti_simple_ternary_inverter_3 (.in_1(in[7:6]), .jo1____1oj(out_6x___jo1____10j[7:6]));
  STI_Simple_Ternary_Inverter sti_simple_ternary_inverter_4 (.in_1(in[5:4]), .jo1____1oj(out_6x___jo1____10j[5:4]));
  STI_Simple_Ternary_Inverter sti_simple_ternary_inverter_5 (.in_1(in[3:2]), .jo1____1oj(out_6x___jo1____10j[3:2]));
  STI_Simple_Ternary_Inverter sti_simple_ternary_inverter_6 (.in_1(in[1:0]), .jo1____1oj(out_6x___jo1____10j[1:0]));
endmodule

module _6t_3_1_MUX (
  input  [11:0] in_1,
  input  [11:0] in_2,
  input  [11:0] in_3,
  input  [1:0] in_4,
  output [11:0] out_5
);

  _3_1_MUX u_3_1_mux_1 (
    .In1(in_1[11:10]), .In0(in_2[11:10]), .Inj(in_3[11:10]), .select(in_4), .\output (out_5[11:10]));
  _3_1_MUX u_3_1_mux_2 (.In1(in_1[9:8]), .In0(in_2[9:8]), .Inj(in_3[9:8]), .select(in_4), .\output (out_5[9:8]));
  _3_1_MUX u_3_1_mux_3 (.In1(in_1[7:6]), .In0(in_2[7:6]), .Inj(in_3[7:6]), .select(in_4), .\output (out_5[7:6]));
  _3_1_MUX u_3_1_mux_4 (.In1(in_1[5:4]), .In0(in_2[5:4]), .Inj(in_3[5:4]), .select(in_4), .\output (out_5[5:4]));
  _3_1_MUX u_3_1_mux_5 (.In1(in_1[3:2]), .In0(in_2[3:2]), .Inj(in_3[3:2]), .select(in_4), .\output (out_5[3:2]));
  _3_1_MUX u_3_1_mux_6 (.In1(in_1[1:0]), .In0(in_2[1:0]), .Inj(in_3[1:0]), .select(in_4), .\output (out_5[1:0]));
endmodule

module _6t_Register (
  input  [11:0] D,
  input  [1:0] clock,
  output [11:0] Q
);

  Register__master_slave_D_latch register_master_slave_d_latch_1 (
    .Clock__pulse__latch_in_on_rising_edge__out_on_falling(clock), .D(D[11:10]), .Q(Q[11:10]));
  Register__master_slave_D_latch register_master_slave_d_latch_2 (
    .Clock__pulse__latch_in_on_rising_edge__out_on_falling(clock), .D(D[9:8]), .Q(Q[9:8]));
  Register__master_slave_D_latch register_master_slave_d_latch_3 (
    .Clock__pulse__latch_in_on_rising_edge__out_on_falling(clock), .D(D[7:6]), .Q(Q[7:6]));
  Register__master_slave_D_latch register_master_slave_d_latch_4 (
    .Clock__pulse__latch_in_on_rising_edge__out_on_falling(clock), .D(D[5:4]), .Q(Q[5:4]));
  Register__master_slave_D_latch register_master_slave_d_latch_5 (
    .Clock__pulse__latch_in_on_rising_edge__out_on_falling(clock), .D(D[3:2]), .Q(Q[3:2]));
  Register__master_slave_D_latch register_master_slave_d_latch_6 (
    .Clock__pulse__latch_in_on_rising_edge__out_on_falling(clock), .D(D[1:0]), .Q(Q[1:0]));
endmodule

module _6t_Register_w_Async_Reset (
  input  [11:0] D,
  input  [1:0] clock,
  input  [1:0] clock_2,
  output [11:0] Q
);

  Register_w_Async_Reset__master_slave_D_latch register_w_async_reset_master_slave_d_latch_1 (
    .D(D[11:10]), .Clock__pulse__latch_in_on_rising_edge__out_on_falling(clock),
    .Reset__Q__1_when_Reset_1__async(clock_2), .Q(Q[11:10]));
  Register_w_Async_Reset__master_slave_D_latch register_w_async_reset_master_slave_d_latch_2 (
    .D(D[9:8]), .Clock__pulse__latch_in_on_rising_edge__out_on_falling(clock),
    .Reset__Q__1_when_Reset_1__async(clock_2), .Q(Q[9:8]));
  Register_w_Async_Reset__master_slave_D_latch register_w_async_reset_master_slave_d_latch_3 (
    .D(D[7:6]), .Clock__pulse__latch_in_on_rising_edge__out_on_falling(clock),
    .Reset__Q__1_when_Reset_1__async(clock_2), .Q(Q[7:6]));
  Register_w_Async_Reset__master_slave_D_latch register_w_async_reset_master_slave_d_latch_4 (
    .D(D[5:4]), .Clock__pulse__latch_in_on_rising_edge__out_on_falling(clock),
    .Reset__Q__1_when_Reset_1__async(clock_2), .Q(Q[5:4]));
  Register_w_Async_Reset__master_slave_D_latch register_w_async_reset_master_slave_d_latch_5 (
    .D(D[3:2]), .Clock__pulse__latch_in_on_rising_edge__out_on_falling(clock),
    .Reset__Q__1_when_Reset_1__async(clock_2), .Q(Q[3:2]));
  Register_w_Async_Reset__master_slave_D_latch register_w_async_reset_master_slave_d_latch_6 (
    .D(D[1:0]), .Clock__pulse__latch_in_on_rising_edge__out_on_falling(clock),
    .Reset__Q__1_when_Reset_1__async(clock_2), .Q(Q[1:0]));
endmodule

module _6t_x_18_stack (
  input  [1:0] j_pop__1_push__0_nop,
  input  [11:0] in,
  input  [1:0] clock,
  output [11:0] top_of_stack
);

  wire [11:0] multiplexer_1_out, multiplexer_2_out, multiplexer_3_out, multiplexer_4_out, multiplexer_5_out,
       multiplexer_6_out, multiplexer_7_out, multiplexer_8_out, multiplexer_9_out, multiplexer_10_out,
       multiplexer_11_out, multiplexer_12_out, multiplexer_13_out, multiplexer_14_out, multiplexer_15_out,
       multiplexer_16_out, multiplexer_17_out, multiplexer_18_out, n6t_register_2_q, n6t_register_3_q,
       n6t_register_4_q, n6t_register_5_q, n6t_register_6_q, n6t_register_7_q, n6t_register_8_q,
       n6t_register_9_q, n6t_register_10_q, n6t_register_11_q, n6t_register_12_q, n6t_register_13_q,
       n6t_register_14_q, n6t_register_15_q, n6t_register_16_q, n6t_register_17_q, n6t_register_18_q;

  Multiplexer #(.select(2), .width(12)) multiplexer_1 (
    .in0(top_of_stack), .in1(in), .in2(n6t_register_2_q), .in3(top_of_stack), .out(multiplexer_1_out),
    .sel(j_pop__1_push__0_nop));
  _6t_Register u_6t_register_1 (.D(multiplexer_1_out), .clock(clock), .Q(top_of_stack));
  Multiplexer #(.select(2), .width(12)) multiplexer_2 (
    .in0(n6t_register_2_q), .in1(top_of_stack), .in2(n6t_register_3_q), .in3(n6t_register_2_q),
    .out(multiplexer_2_out), .sel(j_pop__1_push__0_nop));
  _6t_Register u_6t_register_2 (.D(multiplexer_2_out), .clock(clock), .Q(n6t_register_2_q));
  Multiplexer #(.select(2), .width(12)) multiplexer_3 (
    .in0(n6t_register_3_q), .in1(n6t_register_2_q), .in2(n6t_register_4_q), .in3(n6t_register_3_q),
    .out(multiplexer_3_out), .sel(j_pop__1_push__0_nop));
  _6t_Register u_6t_register_3 (.D(multiplexer_3_out), .clock(clock), .Q(n6t_register_3_q));
  Multiplexer #(.select(2), .width(12)) multiplexer_4 (
    .in0(n6t_register_4_q), .in1(n6t_register_3_q), .in2(n6t_register_5_q), .in3(n6t_register_4_q),
    .out(multiplexer_4_out), .sel(j_pop__1_push__0_nop));
  _6t_Register u_6t_register_4 (.D(multiplexer_4_out), .clock(clock), .Q(n6t_register_4_q));
  Multiplexer #(.select(2), .width(12)) multiplexer_5 (
    .in0(n6t_register_5_q), .in1(n6t_register_4_q), .in2(n6t_register_6_q), .in3(n6t_register_5_q),
    .out(multiplexer_5_out), .sel(j_pop__1_push__0_nop));
  _6t_Register u_6t_register_5 (.D(multiplexer_5_out), .clock(clock), .Q(n6t_register_5_q));
  Multiplexer #(.select(2), .width(12)) multiplexer_6 (
    .in0(n6t_register_6_q), .in1(n6t_register_5_q), .in2(n6t_register_7_q), .in3(n6t_register_6_q),
    .out(multiplexer_6_out), .sel(j_pop__1_push__0_nop));
  _6t_Register u_6t_register_6 (.D(multiplexer_6_out), .clock(clock), .Q(n6t_register_6_q));
  Multiplexer #(.select(2), .width(12)) multiplexer_7 (
    .in0(n6t_register_7_q), .in1(n6t_register_6_q), .in2(n6t_register_8_q), .in3(n6t_register_7_q),
    .out(multiplexer_7_out), .sel(j_pop__1_push__0_nop));
  _6t_Register u_6t_register_7 (.D(multiplexer_7_out), .clock(clock), .Q(n6t_register_7_q));
  Multiplexer #(.select(2), .width(12)) multiplexer_8 (
    .in0(n6t_register_8_q), .in1(n6t_register_7_q), .in2(n6t_register_9_q), .in3(n6t_register_8_q),
    .out(multiplexer_8_out), .sel(j_pop__1_push__0_nop));
  _6t_Register u_6t_register_8 (.D(multiplexer_8_out), .clock(clock), .Q(n6t_register_8_q));
  Multiplexer #(.select(2), .width(12)) multiplexer_9 (
    .in0(n6t_register_9_q), .in1(n6t_register_8_q), .in2(n6t_register_10_q), .in3(n6t_register_9_q),
    .out(multiplexer_9_out), .sel(j_pop__1_push__0_nop));
  _6t_Register u_6t_register_9 (.D(multiplexer_9_out), .clock(clock), .Q(n6t_register_9_q));
  Multiplexer #(.select(2), .width(12)) multiplexer_10 (
    .in0(n6t_register_10_q), .in1(n6t_register_9_q), .in2(n6t_register_11_q), .in3(n6t_register_10_q),
    .out(multiplexer_10_out), .sel(j_pop__1_push__0_nop));
  _6t_Register u_6t_register_10 (.D(multiplexer_10_out), .clock(clock), .Q(n6t_register_10_q));
  Multiplexer #(.select(2), .width(12)) multiplexer_11 (
    .in0(n6t_register_11_q), .in1(n6t_register_10_q), .in2(n6t_register_12_q), .in3(n6t_register_11_q),
    .out(multiplexer_11_out), .sel(j_pop__1_push__0_nop));
  _6t_Register u_6t_register_11 (.D(multiplexer_11_out), .clock(clock), .Q(n6t_register_11_q));
  Multiplexer #(.select(2), .width(12)) multiplexer_12 (
    .in0(n6t_register_12_q), .in1(n6t_register_11_q), .in2(n6t_register_13_q), .in3(n6t_register_12_q),
    .out(multiplexer_12_out), .sel(j_pop__1_push__0_nop));
  _6t_Register u_6t_register_12 (.D(multiplexer_12_out), .clock(clock), .Q(n6t_register_12_q));
  Multiplexer #(.select(2), .width(12)) multiplexer_13 (
    .in0(n6t_register_13_q), .in1(n6t_register_12_q), .in2(n6t_register_14_q), .in3(n6t_register_13_q),
    .out(multiplexer_13_out), .sel(j_pop__1_push__0_nop));
  _6t_Register u_6t_register_13 (.D(multiplexer_13_out), .clock(clock), .Q(n6t_register_13_q));
  Multiplexer #(.select(2), .width(12)) multiplexer_14 (
    .in0(n6t_register_14_q), .in1(n6t_register_13_q), .in2(n6t_register_15_q), .in3(n6t_register_14_q),
    .out(multiplexer_14_out), .sel(j_pop__1_push__0_nop));
  _6t_Register u_6t_register_14 (.D(multiplexer_14_out), .clock(clock), .Q(n6t_register_14_q));
  Multiplexer #(.select(2), .width(12)) multiplexer_15 (
    .in0(n6t_register_15_q), .in1(n6t_register_14_q), .in2(n6t_register_16_q), .in3(n6t_register_15_q),
    .out(multiplexer_15_out), .sel(j_pop__1_push__0_nop));
  _6t_Register u_6t_register_15 (.D(multiplexer_15_out), .clock(clock), .Q(n6t_register_15_q));
  Multiplexer #(.select(2), .width(12)) multiplexer_16 (
    .in0(n6t_register_16_q), .in1(n6t_register_15_q), .in2(n6t_register_17_q), .in3(n6t_register_16_q),
    .out(multiplexer_16_out), .sel(j_pop__1_push__0_nop));
  _6t_Register u_6t_register_16 (.D(multiplexer_16_out), .clock(clock), .Q(n6t_register_16_q));
  Multiplexer #(.select(2), .width(12)) multiplexer_17 (
    .in0(n6t_register_17_q), .in1(n6t_register_16_q), .in2(n6t_register_18_q), .in3(n6t_register_17_q),
    .out(multiplexer_17_out), .sel(j_pop__1_push__0_nop));
  _6t_Register u_6t_register_17 (.D(multiplexer_17_out), .clock(clock), .Q(n6t_register_17_q));
  Multiplexer #(.select(2), .width(12)) multiplexer_18 (
    .in0(n6t_register_18_q), .in1(n6t_register_17_q), .in2(top_of_stack), .in3(n6t_register_18_q),
    .out(multiplexer_18_out), .sel(j_pop__1_push__0_nop));
  _6t_Register u_6t_register_18 (.D(multiplexer_18_out), .clock(clock), .Q(n6t_register_18_q));

  // Notes on the sheet:
  //   Lazy and cheating to use MUXes here I think.
  //   It is often called a stack, and we usually think about it as a stack, but it's actually a ring.  18 pops in a row is a long slow nop.
endmodule

module _6t_counter (
  input  [1:0] clock,
  input  [1:0] reset__sync,
  output [11:0] out
);

  wire [1:0] cu_cycle_up_1_jo1____o1j, cu_cycle_up_2_jo1____o1j, cu_cycle_up_3_jo1____o1j,
       cu_cycle_up_4_jo1____o1j, cu_cycle_up_5_jo1____o1j, cu_cycle_up_6_jo1____o1j,
       pti_positive_trinary_inverter_1_jo1____11j, pti_positive_trinary_inverter_2_jo1____11j,
       pti_positive_trinary_inverter_3_jo1____11j, pti_positive_trinary_inverter_4_jo1____11j,
       pti_positive_trinary_inverter_5_jo1____11j, pti_positive_trinary_inverter_6_jo1____11j,
       sti_simple_ternary_inverter_1_jo1____1oj, sti_simple_ternary_inverter_2_jo1____1oj,
       sti_simple_ternary_inverter_3_jo1____1oj, sti_simple_ternary_inverter_4_jo1____1oj,
       sti_simple_ternary_inverter_5_jo1____1oj, sti_simple_ternary_inverter_6_jo1____1oj,
       tand_fast_2_input_unsafe_1_out_3, tand_fast_2_input_unsafe_2_out_3, tand_fast_2_input_unsafe_3_out_3,
       tand_fast_2_input_unsafe_4_out_3, tnand_3_input_1_out_4, tnand_3_input_2_out_4, tnand_3_input_3_out_4,
       tnand_3_input_4_out_4, tnand_3_input_5_out_4, tnand_3_input_6_out_4,
       tnand_fast_2_input_unsafe_1_out_3, tnand_fast_2_input_unsafe_2_out_3,
       tnand_fast_2_input_unsafe_3_out_3, tnand_fast_2_input_unsafe_4_out_3,
       tnand_fast_2_input_unsafe_5_out_3, tnand_fast_2_input_unsafe_6_out_3,
       tnand_fast_2_input_unsafe_7_out_3, tnand_fast_2_input_unsafe_8_out_3,
       tnand_fast_2_input_unsafe_9_out_3, tnand_fast_2_input_unsafe_10_out_3;

  PTI_Positive_Trinary_Inverter pti_positive_trinary_inverter_1 (
    .in_1(reset__sync), .jo1____11j(pti_positive_trinary_inverter_1_jo1____11j));
  // Probe on pti_positive_trinary_inverter_1_jo1____11j
  TNAND_fast__2_input__unsafe tnand_fast_2_input_unsafe_1 (
    .in_1(sti_simple_ternary_inverter_1_jo1____1oj), .in_2(cu_cycle_up_1_jo1____o1j),
    .out_3(tnand_fast_2_input_unsafe_1_out_3));
  STI_Simple_Ternary_Inverter sti_simple_ternary_inverter_1 (
    .in_1(pti_positive_trinary_inverter_2_jo1____11j), .jo1____1oj(sti_simple_ternary_inverter_1_jo1____1oj));
  PTI_Positive_Trinary_Inverter pti_positive_trinary_inverter_2 (
    .in_1(tand_fast_2_input_unsafe_1_out_3), .jo1____11j(pti_positive_trinary_inverter_2_jo1____11j));
  Register__master_slave_D_latch register_master_slave_d_latch_1 (
    .Clock__pulse__latch_in_on_rising_edge__out_on_falling(clock), .D(tnand_3_input_1_out_4), .Q(out[11:10]));
  TNAND_3_input tnand_3_input_1 (
    .in_1(tnand_fast_2_input_unsafe_1_out_3), .in_2(pti_positive_trinary_inverter_1_jo1____11j),
    .in_3(tnand_fast_2_input_unsafe_2_out_3), .out_4(tnand_3_input_1_out_4));
  TNAND_fast__2_input__unsafe tnand_fast_2_input_unsafe_2 (
    .in_1(out[11:10]), .in_2(pti_positive_trinary_inverter_2_jo1____11j),
    .out_3(tnand_fast_2_input_unsafe_2_out_3));
  CU_Cycle_Up cu_cycle_up_1 (.in_1(out[11:10]), .jo1____o1j(cu_cycle_up_1_jo1____o1j));
  TAND_fast__2_input__unsafe tand_fast_2_input_unsafe_1 (
    .in_1(tand_fast_2_input_unsafe_2_out_3), .in_2(out[9:8]), .out_3(tand_fast_2_input_unsafe_1_out_3));
  TNAND_3_input tnand_3_input_2 (
    .in_1(tnand_fast_2_input_unsafe_3_out_3), .in_2(pti_positive_trinary_inverter_1_jo1____11j),
    .in_3(tnand_fast_2_input_unsafe_4_out_3), .out_4(tnand_3_input_2_out_4));
  TNAND_fast__2_input__unsafe tnand_fast_2_input_unsafe_3 (
    .in_1(sti_simple_ternary_inverter_2_jo1____1oj), .in_2(cu_cycle_up_2_jo1____o1j),
    .out_3(tnand_fast_2_input_unsafe_3_out_3));
  CU_Cycle_Up cu_cycle_up_2 (.in_1(out[9:8]), .jo1____o1j(cu_cycle_up_2_jo1____o1j));
  STI_Simple_Ternary_Inverter sti_simple_ternary_inverter_2 (
    .in_1(pti_positive_trinary_inverter_3_jo1____11j), .jo1____1oj(sti_simple_ternary_inverter_2_jo1____1oj));
  PTI_Positive_Trinary_Inverter pti_positive_trinary_inverter_3 (
    .in_1(tand_fast_2_input_unsafe_2_out_3), .jo1____11j(pti_positive_trinary_inverter_3_jo1____11j));
  Register__master_slave_D_latch register_master_slave_d_latch_2 (
    .Clock__pulse__latch_in_on_rising_edge__out_on_falling(clock), .D(tnand_3_input_2_out_4), .Q(out[9:8]));
  TNAND_fast__2_input__unsafe tnand_fast_2_input_unsafe_4 (
    .in_1(out[9:8]), .in_2(pti_positive_trinary_inverter_3_jo1____11j),
    .out_3(tnand_fast_2_input_unsafe_4_out_3));
  TAND_fast__2_input__unsafe tand_fast_2_input_unsafe_2 (
    .in_1(tand_fast_2_input_unsafe_3_out_3), .in_2(out[7:6]), .out_3(tand_fast_2_input_unsafe_2_out_3));
  TNAND_3_input tnand_3_input_3 (
    .in_1(tnand_fast_2_input_unsafe_5_out_3), .in_2(pti_positive_trinary_inverter_1_jo1____11j),
    .in_3(tnand_fast_2_input_unsafe_6_out_3), .out_4(tnand_3_input_3_out_4));
  TNAND_fast__2_input__unsafe tnand_fast_2_input_unsafe_5 (
    .in_1(sti_simple_ternary_inverter_3_jo1____1oj), .in_2(cu_cycle_up_3_jo1____o1j),
    .out_3(tnand_fast_2_input_unsafe_5_out_3));
  CU_Cycle_Up cu_cycle_up_3 (.in_1(out[7:6]), .jo1____o1j(cu_cycle_up_3_jo1____o1j));
  STI_Simple_Ternary_Inverter sti_simple_ternary_inverter_3 (
    .in_1(pti_positive_trinary_inverter_4_jo1____11j), .jo1____1oj(sti_simple_ternary_inverter_3_jo1____1oj));
  PTI_Positive_Trinary_Inverter pti_positive_trinary_inverter_4 (
    .in_1(tand_fast_2_input_unsafe_3_out_3), .jo1____11j(pti_positive_trinary_inverter_4_jo1____11j));
  Register__master_slave_D_latch register_master_slave_d_latch_3 (
    .Clock__pulse__latch_in_on_rising_edge__out_on_falling(clock), .D(tnand_3_input_3_out_4), .Q(out[7:6]));
  TNAND_fast__2_input__unsafe tnand_fast_2_input_unsafe_6 (
    .in_1(out[7:6]), .in_2(pti_positive_trinary_inverter_4_jo1____11j),
    .out_3(tnand_fast_2_input_unsafe_6_out_3));
  TAND_fast__2_input__unsafe tand_fast_2_input_unsafe_3 (
    .in_1(tand_fast_2_input_unsafe_4_out_3), .in_2(out[5:4]), .out_3(tand_fast_2_input_unsafe_3_out_3));
  TNAND_3_input tnand_3_input_4 (
    .in_1(tnand_fast_2_input_unsafe_8_out_3), .in_2(pti_positive_trinary_inverter_1_jo1____11j),
    .in_3(tnand_fast_2_input_unsafe_7_out_3), .out_4(tnand_3_input_4_out_4));
  TNAND_fast__2_input__unsafe tnand_fast_2_input_unsafe_7 (
    .in_1(out[5:4]), .in_2(pti_positive_trinary_inverter_5_jo1____11j),
    .out_3(tnand_fast_2_input_unsafe_7_out_3));
  TNAND_fast__2_input__unsafe tnand_fast_2_input_unsafe_8 (
    .in_1(sti_simple_ternary_inverter_4_jo1____1oj), .in_2(cu_cycle_up_4_jo1____o1j),
    .out_3(tnand_fast_2_input_unsafe_8_out_3));
  CU_Cycle_Up cu_cycle_up_4 (.in_1(out[5:4]), .jo1____o1j(cu_cycle_up_4_jo1____o1j));
  STI_Simple_Ternary_Inverter sti_simple_ternary_inverter_4 (
    .in_1(pti_positive_trinary_inverter_5_jo1____11j), .jo1____1oj(sti_simple_ternary_inverter_4_jo1____1oj));
  PTI_Positive_Trinary_Inverter pti_positive_trinary_inverter_5 (
    .in_1(tand_fast_2_input_unsafe_4_out_3), .jo1____11j(pti_positive_trinary_inverter_5_jo1____11j));
  Register__master_slave_D_latch register_master_slave_d_latch_4 (
    .Clock__pulse__latch_in_on_rising_edge__out_on_falling(clock), .D(tnand_3_input_4_out_4), .Q(out[5:4]));
  TNAND_fast__2_input__unsafe tnand_fast_2_input_unsafe_9 (
    .in_1(sti_simple_ternary_inverter_5_jo1____1oj), .in_2(cu_cycle_up_5_jo1____o1j),
    .out_3(tnand_fast_2_input_unsafe_9_out_3));
  STI_Simple_Ternary_Inverter sti_simple_ternary_inverter_5 (
    .in_1(pti_positive_trinary_inverter_6_jo1____11j), .jo1____1oj(sti_simple_ternary_inverter_5_jo1____1oj));
  PTI_Positive_Trinary_Inverter pti_positive_trinary_inverter_6 (
    .in_1(out[1:0]), .jo1____11j(pti_positive_trinary_inverter_6_jo1____11j));
  TAND_fast__2_input__unsafe tand_fast_2_input_unsafe_4 (
    .in_1(out[1:0]), .in_2(out[3:2]), .out_3(tand_fast_2_input_unsafe_4_out_3));
  Register__master_slave_D_latch register_master_slave_d_latch_5 (
    .Clock__pulse__latch_in_on_rising_edge__out_on_falling(clock), .D(tnand_3_input_5_out_4), .Q(out[3:2]));
  TNAND_3_input tnand_3_input_5 (
    .in_1(tnand_fast_2_input_unsafe_9_out_3), .in_2(pti_positive_trinary_inverter_1_jo1____11j),
    .in_3(tnand_fast_2_input_unsafe_10_out_3), .out_4(tnand_3_input_5_out_4));
  TNAND_fast__2_input__unsafe tnand_fast_2_input_unsafe_10 (
    .in_1(out[3:2]), .in_2(pti_positive_trinary_inverter_6_jo1____11j),
    .out_3(tnand_fast_2_input_unsafe_10_out_3));
  CU_Cycle_Up cu_cycle_up_5 (.in_1(out[3:2]), .jo1____o1j(cu_cycle_up_5_jo1____o1j));
  TNAND_3_input tnand_3_input_6 (
    .in_1(sti_simple_ternary_inverter_6_jo1____1oj), .in_2(pti_positive_trinary_inverter_1_jo1____11j),
    .in_3(sti_simple_ternary_inverter_6_jo1____1oj), .out_4(tnand_3_input_6_out_4));
  STI_Simple_Ternary_Inverter sti_simple_ternary_inverter_6 (
    .in_1(cu_cycle_up_6_jo1____o1j), .jo1____1oj(sti_simple_ternary_inverter_6_jo1____1oj));
  CU_Cycle_Up cu_cycle_up_6 (.in_1(out[1:0]), .jo1____o1j(cu_cycle_up_6_jo1____o1j));
  Register__master_slave_D_latch register_master_slave_d_latch_6 (
    .Clock__pulse__latch_in_on_rising_edge__out_on_falling(clock), .D(tnand_3_input_6_out_4), .Q(out[1:0]));

  // Notes on the sheet:
  //   Rather than multi-input gates, this is a chain of gates, so it limits the max clock frequency
endmodule
module _6t_counter_w_async_reset (
  input  [1:0] clock,
  input  [1:0] reset__async,
  output [11:0] out
);

  wire [0:0] clock_1_out;
  wire [1:0] cu_cycle_up_1_jo1____o1j, cu_cycle_up_2_jo1____o1j, cu_cycle_up_3_jo1____o1j,
       cu_cycle_up_4_jo1____o1j, cu_cycle_up_5_jo1____o1j, cu_cycle_up_6_jo1____o1j,
       pti_positive_trinary_inverter_1_jo1____11j, pti_positive_trinary_inverter_2_jo1____11j,
       pti_positive_trinary_inverter_3_jo1____11j, pti_positive_trinary_inverter_4_jo1____11j,
       pti_positive_trinary_inverter_5_jo1____11j, sti_simple_ternary_inverter_1_jo1____1oj,
       sti_simple_ternary_inverter_2_jo1____1oj, sti_simple_ternary_inverter_3_jo1____1oj,
       sti_simple_ternary_inverter_4_jo1____1oj, sti_simple_ternary_inverter_5_jo1____1oj,
       sti_simple_ternary_inverter_6_jo1____1oj, tand_fast_2_input_unsafe_1_out_3,
       tand_fast_2_input_unsafe_2_out_3, tand_fast_2_input_unsafe_3_out_3, tand_fast_2_input_unsafe_4_out_3,
       tnand_fast_2_input_unsafe_1_out_3, tnand_fast_2_input_unsafe_2_out_3,
       tnand_fast_2_input_unsafe_3_out_3, tnand_fast_2_input_unsafe_4_out_3,
       tnand_fast_2_input_unsafe_5_out_3, tnand_fast_2_input_unsafe_6_out_3,
       tnand_fast_2_input_unsafe_7_out_3, tnand_fast_2_input_unsafe_8_out_3,
       tnand_fast_2_input_unsafe_9_out_3, tnand_fast_2_input_unsafe_10_out_3,
       tnand_fast_2_input_unsafe_11_out_3, tnand_fast_2_input_unsafe_12_out_3,
       tnand_fast_2_input_unsafe_13_out_3, tnand_fast_2_input_unsafe_14_out_3,
       tnand_fast_2_input_unsafe_15_out_3, tnand_fast_2_input_unsafe_16_out_3;

  Clock clock_1 (.out(clock_1_out[0]));
  TNAND_fast__2_input__unsafe tnand_fast_2_input_unsafe_1 (
    .in_1(sti_simple_ternary_inverter_1_jo1____1oj), .in_2(cu_cycle_up_1_jo1____o1j),
    .out_3(tnand_fast_2_input_unsafe_1_out_3));
  STI_Simple_Ternary_Inverter sti_simple_ternary_inverter_1 (
    .in_1(pti_positive_trinary_inverter_1_jo1____11j), .jo1____1oj(sti_simple_ternary_inverter_1_jo1____1oj));
  PTI_Positive_Trinary_Inverter pti_positive_trinary_inverter_1 (
    .in_1(tand_fast_2_input_unsafe_1_out_3), .jo1____11j(pti_positive_trinary_inverter_1_jo1____11j));
  Register_w_Async_Reset__master_slave_D_latch register_w_async_reset_master_slave_d_latch_1 (
    .D(tnand_fast_2_input_unsafe_2_out_3), .Clock__pulse__latch_in_on_rising_edge__out_on_falling(clock),
    .Reset__Q__1_when_Reset_1__async(reset__async), .Q(out[11:10]));
  TNAND_fast__2_input__unsafe tnand_fast_2_input_unsafe_2 (
    .in_1(tnand_fast_2_input_unsafe_1_out_3), .in_2(tnand_fast_2_input_unsafe_3_out_3),
    .out_3(tnand_fast_2_input_unsafe_2_out_3));
  TNAND_fast__2_input__unsafe tnand_fast_2_input_unsafe_3 (
    .in_1(out[11:10]), .in_2(pti_positive_trinary_inverter_1_jo1____11j),
    .out_3(tnand_fast_2_input_unsafe_3_out_3));
  CU_Cycle_Up cu_cycle_up_1 (.in_1(out[11:10]), .jo1____o1j(cu_cycle_up_1_jo1____o1j));
  TAND_fast__2_input__unsafe tand_fast_2_input_unsafe_1 (
    .in_1(tand_fast_2_input_unsafe_2_out_3), .in_2(out[9:8]), .out_3(tand_fast_2_input_unsafe_1_out_3));
  TNAND_fast__2_input__unsafe tnand_fast_2_input_unsafe_4 (
    .in_1(tnand_fast_2_input_unsafe_5_out_3), .in_2(tnand_fast_2_input_unsafe_6_out_3),
    .out_3(tnand_fast_2_input_unsafe_4_out_3));
  TNAND_fast__2_input__unsafe tnand_fast_2_input_unsafe_5 (
    .in_1(sti_simple_ternary_inverter_2_jo1____1oj), .in_2(cu_cycle_up_2_jo1____o1j),
    .out_3(tnand_fast_2_input_unsafe_5_out_3));
  CU_Cycle_Up cu_cycle_up_2 (.in_1(out[9:8]), .jo1____o1j(cu_cycle_up_2_jo1____o1j));
  STI_Simple_Ternary_Inverter sti_simple_ternary_inverter_2 (
    .in_1(pti_positive_trinary_inverter_2_jo1____11j), .jo1____1oj(sti_simple_ternary_inverter_2_jo1____1oj));
  PTI_Positive_Trinary_Inverter pti_positive_trinary_inverter_2 (
    .in_1(tand_fast_2_input_unsafe_2_out_3), .jo1____11j(pti_positive_trinary_inverter_2_jo1____11j));
  Register_w_Async_Reset__master_slave_D_latch register_w_async_reset_master_slave_d_latch_2 (
    .D(tnand_fast_2_input_unsafe_4_out_3), .Clock__pulse__latch_in_on_rising_edge__out_on_falling(clock),
    .Reset__Q__1_when_Reset_1__async(reset__async), .Q(out[9:8]));
  TNAND_fast__2_input__unsafe tnand_fast_2_input_unsafe_6 (
    .in_1(out[9:8]), .in_2(pti_positive_trinary_inverter_2_jo1____11j),
    .out_3(tnand_fast_2_input_unsafe_6_out_3));
  TAND_fast__2_input__unsafe tand_fast_2_input_unsafe_2 (
    .in_1(tand_fast_2_input_unsafe_3_out_3), .in_2(out[7:6]), .out_3(tand_fast_2_input_unsafe_2_out_3));
  TNAND_fast__2_input__unsafe tnand_fast_2_input_unsafe_7 (
    .in_1(tnand_fast_2_input_unsafe_8_out_3), .in_2(tnand_fast_2_input_unsafe_9_out_3),
    .out_3(tnand_fast_2_input_unsafe_7_out_3));
  TNAND_fast__2_input__unsafe tnand_fast_2_input_unsafe_8 (
    .in_1(sti_simple_ternary_inverter_3_jo1____1oj), .in_2(cu_cycle_up_3_jo1____o1j),
    .out_3(tnand_fast_2_input_unsafe_8_out_3));
  CU_Cycle_Up cu_cycle_up_3 (.in_1(out[7:6]), .jo1____o1j(cu_cycle_up_3_jo1____o1j));
  STI_Simple_Ternary_Inverter sti_simple_ternary_inverter_3 (
    .in_1(pti_positive_trinary_inverter_3_jo1____11j), .jo1____1oj(sti_simple_ternary_inverter_3_jo1____1oj));
  PTI_Positive_Trinary_Inverter pti_positive_trinary_inverter_3 (
    .in_1(tand_fast_2_input_unsafe_3_out_3), .jo1____11j(pti_positive_trinary_inverter_3_jo1____11j));
  Register_w_Async_Reset__master_slave_D_latch register_w_async_reset_master_slave_d_latch_3 (
    .D(tnand_fast_2_input_unsafe_7_out_3), .Clock__pulse__latch_in_on_rising_edge__out_on_falling(clock),
    .Reset__Q__1_when_Reset_1__async(reset__async), .Q(out[7:6]));
  TNAND_fast__2_input__unsafe tnand_fast_2_input_unsafe_9 (
    .in_1(out[7:6]), .in_2(pti_positive_trinary_inverter_3_jo1____11j),
    .out_3(tnand_fast_2_input_unsafe_9_out_3));
  TAND_fast__2_input__unsafe tand_fast_2_input_unsafe_3 (
    .in_1(tand_fast_2_input_unsafe_4_out_3), .in_2(out[5:4]), .out_3(tand_fast_2_input_unsafe_3_out_3));
  Register_w_Async_Reset__master_slave_D_latch register_w_async_reset_master_slave_d_latch_4 (
    .D(tnand_fast_2_input_unsafe_10_out_3), .Clock__pulse__latch_in_on_rising_edge__out_on_falling(clock),
    .Reset__Q__1_when_Reset_1__async(reset__async), .Q(out[5:4]));
  TNAND_fast__2_input__unsafe tnand_fast_2_input_unsafe_10 (
    .in_1(tnand_fast_2_input_unsafe_12_out_3), .in_2(tnand_fast_2_input_unsafe_11_out_3),
    .out_3(tnand_fast_2_input_unsafe_10_out_3));
  TNAND_fast__2_input__unsafe tnand_fast_2_input_unsafe_11 (
    .in_1(out[5:4]), .in_2(pti_positive_trinary_inverter_4_jo1____11j),
    .out_3(tnand_fast_2_input_unsafe_11_out_3));
  TNAND_fast__2_input__unsafe tnand_fast_2_input_unsafe_12 (
    .in_1(sti_simple_ternary_inverter_4_jo1____1oj), .in_2(cu_cycle_up_4_jo1____o1j),
    .out_3(tnand_fast_2_input_unsafe_12_out_3));
  CU_Cycle_Up cu_cycle_up_4 (.in_1(out[5:4]), .jo1____o1j(cu_cycle_up_4_jo1____o1j));
  STI_Simple_Ternary_Inverter sti_simple_ternary_inverter_4 (
    .in_1(pti_positive_trinary_inverter_4_jo1____11j), .jo1____1oj(sti_simple_ternary_inverter_4_jo1____1oj));
  PTI_Positive_Trinary_Inverter pti_positive_trinary_inverter_4 (
    .in_1(tand_fast_2_input_unsafe_4_out_3), .jo1____11j(pti_positive_trinary_inverter_4_jo1____11j));
  TNAND_fast__2_input__unsafe tnand_fast_2_input_unsafe_13 (
    .in_1(sti_simple_ternary_inverter_5_jo1____1oj), .in_2(cu_cycle_up_5_jo1____o1j),
    .out_3(tnand_fast_2_input_unsafe_13_out_3));
  STI_Simple_Ternary_Inverter sti_simple_ternary_inverter_5 (
    .in_1(pti_positive_trinary_inverter_5_jo1____11j), .jo1____1oj(sti_simple_ternary_inverter_5_jo1____1oj));
  PTI_Positive_Trinary_Inverter pti_positive_trinary_inverter_5 (
    .in_1(out[1:0]), .jo1____11j(pti_positive_trinary_inverter_5_jo1____11j));
  TAND_fast__2_input__unsafe tand_fast_2_input_unsafe_4 (
    .in_1(out[1:0]), .in_2(out[3:2]), .out_3(tand_fast_2_input_unsafe_4_out_3));
  Register_w_Async_Reset__master_slave_D_latch register_w_async_reset_master_slave_d_latch_5 (
    .D(tnand_fast_2_input_unsafe_14_out_3), .Clock__pulse__latch_in_on_rising_edge__out_on_falling(clock),
    .Reset__Q__1_when_Reset_1__async(reset__async), .Q(out[3:2]));
  TNAND_fast__2_input__unsafe tnand_fast_2_input_unsafe_14 (
    .in_1(tnand_fast_2_input_unsafe_13_out_3), .in_2(tnand_fast_2_input_unsafe_15_out_3),
    .out_3(tnand_fast_2_input_unsafe_14_out_3));
  TNAND_fast__2_input__unsafe tnand_fast_2_input_unsafe_15 (
    .in_1(out[3:2]), .in_2(pti_positive_trinary_inverter_5_jo1____11j),
    .out_3(tnand_fast_2_input_unsafe_15_out_3));
  CU_Cycle_Up cu_cycle_up_5 (.in_1(out[3:2]), .jo1____o1j(cu_cycle_up_5_jo1____o1j));
  TNAND_fast__2_input__unsafe tnand_fast_2_input_unsafe_16 (
    .in_1(sti_simple_ternary_inverter_6_jo1____1oj), .in_2(sti_simple_ternary_inverter_6_jo1____1oj),
    .out_3(tnand_fast_2_input_unsafe_16_out_3));
  STI_Simple_Ternary_Inverter sti_simple_ternary_inverter_6 (
    .in_1(cu_cycle_up_6_jo1____o1j), .jo1____1oj(sti_simple_ternary_inverter_6_jo1____1oj));
  CU_Cycle_Up cu_cycle_up_6 (.in_1(out[1:0]), .jo1____o1j(cu_cycle_up_6_jo1____o1j));
  Register_w_Async_Reset__master_slave_D_latch register_w_async_reset_master_slave_d_latch_6 (
    .D(tnand_fast_2_input_unsafe_16_out_3), .Clock__pulse__latch_in_on_rising_edge__out_on_falling(clock),
    .Reset__Q__1_when_Reset_1__async(reset__async), .Q(out[1:0]));

  // Notes on the sheet:
  //   Rather than multi-input gates, this is a chain of gates, so it limits the max clock frequency
endmodule

module _6t_ripple_carry_adder (
  input  [11:0] in_1,
  input  [11:0] in_2,
  input  [1:0] in_3,
  output [11:0] out_4,
  output [1:0] out_5
);

  wire [1:0] n1t_full_adder_1_carry_out, n1t_full_adder_2_carry_out, n1t_full_adder_3_carry_out,
       n1t_full_adder_4_carry_out, n1t_full_adder_5_carry_out;

  _1t_full_adder u_1t_full_adder_1 (
    .A(in_1[1:0]), .B(in_2[1:0]), .C(in_3), .Carry_out(n1t_full_adder_1_carry_out), .Sum_out(out_4[1:0]));
  _1t_full_adder u_1t_full_adder_2 (
    .A(in_1[3:2]), .B(in_2[3:2]), .C(n1t_full_adder_1_carry_out), .Carry_out(n1t_full_adder_2_carry_out),
    .Sum_out(out_4[3:2]));
  _1t_full_adder u_1t_full_adder_3 (
    .A(in_1[5:4]), .B(in_2[5:4]), .C(n1t_full_adder_2_carry_out), .Carry_out(n1t_full_adder_3_carry_out),
    .Sum_out(out_4[5:4]));
  _1t_full_adder u_1t_full_adder_4 (
    .A(in_1[7:6]), .B(in_2[7:6]), .C(n1t_full_adder_3_carry_out), .Carry_out(n1t_full_adder_4_carry_out),
    .Sum_out(out_4[7:6]));
  _1t_full_adder u_1t_full_adder_5 (
    .A(in_1[9:8]), .B(in_2[9:8]), .C(n1t_full_adder_4_carry_out), .Carry_out(n1t_full_adder_5_carry_out),
    .Sum_out(out_4[9:8]));
  _1t_full_adder u_1t_full_adder_6 (
    .A(in_1[11:10]), .B(in_2[11:10]), .C(n1t_full_adder_5_carry_out), .Carry_out(out_5),
    .Sum_out(out_4[11:10]));
endmodule

module _2t_to_7seg_driver (
  input  [3:0] in_1,
  output out_2,
  output out_3,
  output out_4,
  output out_5,
  output out_6,
  output out_7,
  output out_8,
  output out_9
);

  ROM #(.addrWidth(4)) rom_1 (
    .addr(in_1), .data({out_9, out_8, out_7, out_6, out_5, out_4, out_3, out_2}));  // open: sel

  // Notes on the sheet:
  //   contents of rom_1 (hex, n*v repeats v):
  //   fc 60 ee fc f2 66 da f2 9c 3e 7a 9c fc 60 ee fc
endmodule

module keyboard_input (
  input  in_1,
  input  in_2,
  input  in_3,
  input  in_4,
  input  in_5,
  input  in_6,
  input  in_7,
  input  in_8,
  input  in_9,
  output [11:0] out_10
);

  wire or_2_out;
  wire [0:0] or_7_out;
  wire [1:0] or_1_out, or_4_out, pti_positive_trinary_inverter_1_jo1____11j;

  // Probe on out_10[11:10]
  Register__master_slave_D_latch register_master_slave_d_latch_1 (
    .Clock__pulse__latch_in_on_rising_edge__out_on_falling(pti_positive_trinary_inverter_1_jo1____11j),
    .D(out_10[7:6]), .Q(out_10[11:10]));
  // Probe on out_10[9:8]
  Register__master_slave_D_latch register_master_slave_d_latch_2 (
    .Clock__pulse__latch_in_on_rising_edge__out_on_falling(pti_positive_trinary_inverter_1_jo1____11j),
    .D(out_10[5:4]), .Q(out_10[9:8]));
  // Probe on out_10[7:6]
  Register__master_slave_D_latch register_master_slave_d_latch_3 (
    .Clock__pulse__latch_in_on_rising_edge__out_on_falling(pti_positive_trinary_inverter_1_jo1____11j),
    .D(out_10[3:2]), .Q(out_10[7:6]));
  // Probe on out_10[5:4]
  Register__master_slave_D_latch register_master_slave_d_latch_4 (
    .Clock__pulse__latch_in_on_rising_edge__out_on_falling(pti_positive_trinary_inverter_1_jo1____11j),
    .D(out_10[1:0]), .Q(out_10[5:4]));
  // Probe on out_10[3:2]
  Register__master_slave_D_latch register_master_slave_d_latch_5 (
    .Clock__pulse__latch_in_on_rising_edge__out_on_falling(pti_positive_trinary_inverter_1_jo1____11j),
    .D(or_1_out), .Q(out_10[3:2]));
  Register__master_slave_D_latch register_master_slave_d_latch_6 (
    .Clock__pulse__latch_in_on_rising_edge__out_on_falling(pti_positive_trinary_inverter_1_jo1____11j),
    .D(or_4_out), .Q(out_10[1:0]));
  // Probe on out_10[1:0]
  PTI_Positive_Trinary_Inverter pti_positive_trinary_inverter_1 (
    .in_1({1'b0, or_7_out[0]}), .jo1____11j(pti_positive_trinary_inverter_1_jo1____11j));
  or or_1 (or_1_out[0], in_1, in_2, in_3);
  or or_2 (or_2_out, in_4, in_5, in_6);
  or or_3 (or_1_out[1], in_7, in_8, in_9);
  or or_4 (or_4_out[0], in_3, in_6, in_9);
  // OR_Gate or_5 has open pins: in1=in_2, in2=in_5, in3=in_8, out=open
  or or_6 (or_4_out[1], in_1, in_4, in_7);
  or or_7 (or_7_out[0], or_1_out[0], or_2_out, or_1_out[1]);
endmodule

module tri_led_driver (
  input  [1:0] in_1,
  output out_2,
  output out_3,
  output out_4
);

  wire decoder_1_out0, decoder_1_out3;

  Decoder #(.select(2)) decoder_1 (
    .out0(decoder_1_out0), .out1(out_2), .out2(out_4), .out3(decoder_1_out3), .sel(in_1));
  or or_1 (out_3, decoder_1_out0, decoder_1_out3);
endmodule

module rs_latch_notes (
  input  [1:0] in_1,
  input  [1:0] in_2,
  input  [1:0] in_3,
  input  [1:0] in_4,
  input  [1:0] in_5,
  input  [1:0] in_6,
  input  [1:0] in_7,
  input  [1:0] in_8,
  input  [1:0] in_9
);

  wire tri_led_driver_1_out_2, tri_led_driver_1_out_3, tri_led_driver_1_out_4, tri_led_driver_2_out_2,
       tri_led_driver_2_out_3, tri_led_driver_2_out_4, tri_led_driver_3_out_2, tri_led_driver_3_out_3,
       tri_led_driver_3_out_4, tri_led_driver_4_out_2, tri_led_driver_4_out_3, tri_led_driver_4_out_4,
       tri_led_driver_5_out_2, tri_led_driver_5_out_3, tri_led_driver_5_out_4, tri_led_driver_6_out_2,
       tri_led_driver_6_out_3, tri_led_driver_6_out_4, tri_led_driver_7_out_2, tri_led_driver_7_out_3,
       tri_led_driver_7_out_4, tri_led_driver_8_out_2, tri_led_driver_8_out_3, tri_led_driver_8_out_4,
       tri_led_driver_9_out_2, tri_led_driver_9_out_3, tri_led_driver_9_out_4, tri_led_driver_10_out_2,
       tri_led_driver_10_out_3, tri_led_driver_10_out_4, tri_led_driver_11_out_2, tri_led_driver_11_out_3,
       tri_led_driver_11_out_4, tri_led_driver_12_out_2, tri_led_driver_12_out_3, tri_led_driver_12_out_4,
       tri_led_driver_13_out_2, tri_led_driver_13_out_3, tri_led_driver_13_out_4, tri_led_driver_14_out_2,
       tri_led_driver_14_out_3, tri_led_driver_14_out_4, tri_led_driver_15_out_2, tri_led_driver_15_out_3,
       tri_led_driver_15_out_4, tri_led_driver_16_out_2, tri_led_driver_16_out_3, tri_led_driver_16_out_4,
       tri_led_driver_17_out_2, tri_led_driver_17_out_3, tri_led_driver_17_out_4, tri_led_driver_18_out_2,
       tri_led_driver_18_out_3, tri_led_driver_18_out_4;
  wire [1:0] nti_negative_trinary_inverter_1_jo1____1jj, nti_negative_trinary_inverter_2_jo1____1jj,
       tand_min_3_input_1_out_4, tand_min_3_input_2_out_4, tnand_3_input_1_out_4, tnand_3_input_2_out_4,
       tnand_3_input_3_out_4, tnand_3_input_4_out_4, tnand_3_input_5_out_4, tnor_3_input_1_out_4,
       tnor_3_input_2_out_4;

  LED led_1 (.in(tri_led_driver_1_out_2));
  LED led_2 (.in(tri_led_driver_1_out_3));
  tri_led_driver tri_led_driver_1 (
    .in_1(in_2), .out_2(tri_led_driver_1_out_2), .out_3(tri_led_driver_1_out_3),
    .out_4(tri_led_driver_1_out_4));
  LED led_3 (.in(tri_led_driver_1_out_4));
  LED led_4 (.in(tri_led_driver_2_out_2));
  LED led_5 (.in(tri_led_driver_2_out_3));
  tri_led_driver tri_led_driver_2 (
    .in_1(in_3), .out_2(tri_led_driver_2_out_2), .out_3(tri_led_driver_2_out_3),
    .out_4(tri_led_driver_2_out_4));
  LED led_6 (.in(tri_led_driver_2_out_4));
  LED led_7 (.in(tri_led_driver_3_out_2));
  LED led_8 (.in(tri_led_driver_3_out_3));
  tri_led_driver tri_led_driver_3 (
    .in_1(in_6), .out_2(tri_led_driver_3_out_2), .out_3(tri_led_driver_3_out_3),
    .out_4(tri_led_driver_3_out_4));
  LED led_9 (.in(tri_led_driver_3_out_4));
  LED led_10 (.in(tri_led_driver_4_out_2));
  LED led_11 (.in(tri_led_driver_4_out_3));
  tri_led_driver tri_led_driver_4 (
    .in_1(in_7), .out_2(tri_led_driver_4_out_2), .out_3(tri_led_driver_4_out_3),
    .out_4(tri_led_driver_4_out_4));
  LED led_12 (.in(tri_led_driver_4_out_4));
  LED led_13 (.in(tri_led_driver_5_out_2));
  LED led_14 (.in(tri_led_driver_5_out_3));
  tri_led_driver tri_led_driver_5 (
    .in_1(in_8), .out_2(tri_led_driver_5_out_2), .out_3(tri_led_driver_5_out_3),
    .out_4(tri_led_driver_5_out_4));
  LED led_15 (.in(tri_led_driver_5_out_4));
  LED led_16 (.in(tri_led_driver_6_out_2));
  LED led_17 (.in(tri_led_driver_6_out_3));
  tri_led_driver tri_led_driver_6 (
    .in_1(in_9), .out_2(tri_led_driver_6_out_2), .out_3(tri_led_driver_6_out_3),
    .out_4(tri_led_driver_6_out_4));
  LED led_18 (.in(tri_led_driver_6_out_4));
  TNAND_3_input tnand_3_input_1 (.in_1(tnand_3_input_2_out_4), .in_2(in_2), .in_3(in_2), .out_4(tnand_3_input_1_out_4));
  TNAND_3_input tnand_3_input_2 (.in_1(in_3), .in_2(in_3), .in_3(tnand_3_input_1_out_4), .out_4(tnand_3_input_2_out_4));
  TAND__min__3_input tand_min_3_input_1 (
    .in_1(nti_negative_trinary_inverter_2_jo1____1jj), .in_2(in_6), .in_3(in_6),
    .out_4(tand_min_3_input_1_out_4));
  TAND__min__3_input tand_min_3_input_2 (
    .in_1(in_7), .in_2(in_7), .in_3(nti_negative_trinary_inverter_1_jo1____1jj),
    .out_4(tand_min_3_input_2_out_4));
  TNOR_3_input tnor_3_input_1 (.in_1(tnor_3_input_2_out_4), .in_2(in_8), .in_3(in_8), .out_4(tnor_3_input_1_out_4));
  TNOR_3_input tnor_3_input_2 (.in_1(in_9), .in_2(in_9), .in_3(tnor_3_input_1_out_4), .out_4(tnor_3_input_2_out_4));
  NTI_Negative_Trinary_Inverter nti_negative_trinary_inverter_1 (
    .in_1(tand_min_3_input_1_out_4), .jo1____1jj(nti_negative_trinary_inverter_1_jo1____1jj));
  NTI_Negative_Trinary_Inverter nti_negative_trinary_inverter_2 (
    .in_1(tand_min_3_input_2_out_4), .jo1____1jj(nti_negative_trinary_inverter_2_jo1____1jj));
  LED led_19 (.in(tri_led_driver_7_out_2));
  tri_led_driver tri_led_driver_7 (
    .in_1(tnand_3_input_1_out_4), .out_2(tri_led_driver_7_out_2), .out_3(tri_led_driver_7_out_3),
    .out_4(tri_led_driver_7_out_4));
  LED led_20 (.in(tri_led_driver_7_out_3));
  LED led_21 (.in(tri_led_driver_7_out_4));
  LED led_22 (.in(tri_led_driver_8_out_2));
  LED led_23 (.in(tri_led_driver_8_out_3));
  tri_led_driver tri_led_driver_8 (
    .in_1(tnand_3_input_2_out_4), .out_2(tri_led_driver_8_out_2), .out_3(tri_led_driver_8_out_3),
    .out_4(tri_led_driver_8_out_4));
  LED led_24 (.in(tri_led_driver_8_out_4));
  LED led_25 (.in(tri_led_driver_9_out_2));
  tri_led_driver tri_led_driver_9 (
    .in_1(nti_negative_trinary_inverter_1_jo1____1jj), .out_2(tri_led_driver_9_out_2),
    .out_3(tri_led_driver_9_out_3), .out_4(tri_led_driver_9_out_4));
  LED led_26 (.in(tri_led_driver_9_out_3));
  LED led_27 (.in(tri_led_driver_9_out_4));
  LED led_28 (.in(tri_led_driver_10_out_2));
  tri_led_driver tri_led_driver_10 (
    .in_1(nti_negative_trinary_inverter_2_jo1____1jj), .out_2(tri_led_driver_10_out_2),
    .out_3(tri_led_driver_10_out_3), .out_4(tri_led_driver_10_out_4));
  LED led_29 (.in(tri_led_driver_10_out_3));
  LED led_30 (.in(tri_led_driver_10_out_4));
  LED led_31 (.in(tri_led_driver_11_out_2));
  tri_led_driver tri_led_driver_11 (
    .in_1(tnor_3_input_1_out_4), .out_2(tri_led_driver_11_out_2), .out_3(tri_led_driver_11_out_3),
    .out_4(tri_led_driver_11_out_4));
  LED led_32 (.in(tri_led_driver_11_out_3));
  LED led_33 (.in(tri_led_driver_11_out_4));
  LED led_34 (.in(tri_led_driver_12_out_2));
  tri_led_driver tri_led_driver_12 (
    .in_1(tnor_3_input_2_out_4), .out_2(tri_led_driver_12_out_2), .out_3(tri_led_driver_12_out_3),
    .out_4(tri_led_driver_12_out_4));
  LED led_35 (.in(tri_led_driver_12_out_3));
  LED led_36 (.in(tri_led_driver_12_out_4));
  LED led_37 (.in(tri_led_driver_13_out_2));
  LED led_38 (.in(tri_led_driver_13_out_4));
  LED led_39 (.in(tri_led_driver_14_out_2));
  LED led_40 (.in(tri_led_driver_14_out_4));
  LED led_41 (.in(tri_led_driver_15_out_2));
  LED led_42 (.in(tri_led_driver_15_out_4));
  LED led_43 (.in(tri_led_driver_13_out_3));
  tri_led_driver tri_led_driver_13 (
    .in_1(in_1), .out_2(tri_led_driver_13_out_2), .out_3(tri_led_driver_13_out_3),
    .out_4(tri_led_driver_13_out_4));
  tri_led_driver tri_led_driver_14 (
    .in_1(in_4), .out_2(tri_led_driver_14_out_2), .out_3(tri_led_driver_14_out_3),
    .out_4(tri_led_driver_14_out_4));
  LED led_44 (.in(tri_led_driver_14_out_3));
  LED led_45 (.in(tri_led_driver_15_out_3));
  tri_led_driver tri_led_driver_15 (
    .in_1(in_5), .out_2(tri_led_driver_15_out_2), .out_3(tri_led_driver_15_out_3),
    .out_4(tri_led_driver_15_out_4));
  TNAND_3_input tnand_3_input_3 (.in_1(in_1), .in_2(in_1), .in_3(tnand_3_input_4_out_4), .out_4(tnand_3_input_3_out_4));
  TNAND_3_input tnand_3_input_4 (.in_1(in_4), .in_2(in_4), .in_3(tnand_3_input_5_out_4), .out_4(tnand_3_input_4_out_4));
  TNAND_3_input tnand_3_input_5 (.in_1(in_5), .in_2(in_5), .in_3(tnand_3_input_3_out_4), .out_4(tnand_3_input_5_out_4));
  LED led_46 (.in(tri_led_driver_16_out_2));
  tri_led_driver tri_led_driver_16 (
    .in_1(tnand_3_input_3_out_4), .out_2(tri_led_driver_16_out_2), .out_3(tri_led_driver_16_out_3),
    .out_4(tri_led_driver_16_out_4));
  LED led_47 (.in(tri_led_driver_16_out_3));
  LED led_48 (.in(tri_led_driver_16_out_4));
  LED led_49 (.in(tri_led_driver_17_out_2));
  tri_led_driver tri_led_driver_17 (
    .in_1(tnand_3_input_4_out_4), .out_2(tri_led_driver_17_out_2), .out_3(tri_led_driver_17_out_3),
    .out_4(tri_led_driver_17_out_4));
  LED led_50 (.in(tri_led_driver_17_out_3));
  LED led_51 (.in(tri_led_driver_17_out_4));
  LED led_52 (.in(tri_led_driver_18_out_2));
  LED led_53 (.in(tri_led_driver_18_out_3));
  tri_led_driver tri_led_driver_18 (
    .in_1(tnand_3_input_5_out_4), .out_2(tri_led_driver_18_out_2), .out_3(tri_led_driver_18_out_3),
    .out_4(tri_led_driver_18_out_4));
  LED led_54 (.in(tri_led_driver_18_out_4));

  // Notes on the sheet:
  //   This doesn't work.  Idle in 1, doesn't show latch behavior unless move one input to -1
  //   But in that case 'glitches' to 0 before latching to -1
  //   But, is incomplete because it only has 2 stable states
  //   This does.  Idle in 0 or 1, latches when an input transitions to -1.
  //   Both -1 acts as a nor-rs latch, just shows 1 on both outputs
endmodule

module Muller_C_gate_notes (
  input  [1:0] in_1,
  input  [1:0] in_2,
  output [1:0] out_3
);

  wire tri_led_driver_1_out_2, tri_led_driver_1_out_3, tri_led_driver_1_out_4, tri_led_driver_2_out_2,
       tri_led_driver_2_out_3, tri_led_driver_2_out_4, tri_led_driver_3_out_2, tri_led_driver_3_out_3,
       tri_led_driver_3_out_4, tri_led_driver_4_out_2, tri_led_driver_4_out_3, tri_led_driver_4_out_4,
       tri_led_driver_5_out_2, tri_led_driver_5_out_3, tri_led_driver_5_out_4, tri_led_driver_6_out_2,
       tri_led_driver_6_out_3, tri_led_driver_6_out_4;
  wire [1:0] tnand_3_input_1_out_4, tnand_3_input_2_out_4, tnand_3_input_3_out_4;

  LED led_1 (.in(tri_led_driver_1_out_4));
  LED led_2 (.in(tri_led_driver_2_out_4));
  LED led_3 (.in(tri_led_driver_1_out_2));
  tri_led_driver tri_led_driver_1 (
    .in_1(in_1), .out_2(tri_led_driver_1_out_2), .out_3(tri_led_driver_1_out_3),
    .out_4(tri_led_driver_1_out_4));
  LED led_4 (.in(tri_led_driver_1_out_3));
  LED led_5 (.in(tri_led_driver_2_out_2));
  LED led_6 (.in(tri_led_driver_2_out_3));
  tri_led_driver tri_led_driver_2 (
    .in_1(in_2), .out_2(tri_led_driver_2_out_2), .out_3(tri_led_driver_2_out_3),
    .out_4(tri_led_driver_2_out_4));
  TNAND_3_input tnand_3_input_1 (.in_1(out_3), .in_2(out_3), .in_3(in_1), .out_4(tnand_3_input_1_out_4));
  LED led_7 (.in(tri_led_driver_3_out_2));
  LED led_8 (.in(tri_led_driver_3_out_4));
  LED led_9 (.in(tri_led_driver_3_out_3));
  tri_led_driver tri_led_driver_3 (
    .in_1(tnand_3_input_1_out_4), .out_2(tri_led_driver_3_out_2), .out_3(tri_led_driver_3_out_3),
    .out_4(tri_led_driver_3_out_4));
  TNAND_3_input tnand_3_input_2 (.in_1(in_1), .in_2(in_1), .in_3(in_2), .out_4(tnand_3_input_2_out_4));
  LED led_10 (.in(tri_led_driver_4_out_2));
  LED led_11 (.in(tri_led_driver_4_out_4));
  LED led_12 (.in(tri_led_driver_4_out_3));
  tri_led_driver tri_led_driver_4 (
    .in_1(tnand_3_input_2_out_4), .out_2(tri_led_driver_4_out_2), .out_3(tri_led_driver_4_out_3),
    .out_4(tri_led_driver_4_out_4));
  TNAND_3_input tnand_3_input_3 (.in_1(in_2), .in_2(in_2), .in_3(out_3), .out_4(tnand_3_input_3_out_4));
  LED led_13 (.in(tri_led_driver_5_out_2));
  LED led_14 (.in(tri_led_driver_5_out_4));
  tri_led_driver tri_led_driver_5 (
    .in_1(tnand_3_input_3_out_4), .out_2(tri_led_driver_5_out_2), .out_3(tri_led_driver_5_out_3),
    .out_4(tri_led_driver_5_out_4));
  LED led_15 (.in(tri_led_driver_5_out_3));
  TNAND_3_input tnand_3_input_4 (
    .in_1(tnand_3_input_1_out_4), .in_2(tnand_3_input_2_out_4), .in_3(tnand_3_input_3_out_4), .out_4(out_3));
  LED led_16 (.in(tri_led_driver_6_out_4));
  LED led_17 (.in(tri_led_driver_6_out_2));
  tri_led_driver tri_led_driver_6 (
    .in_1(out_3), .out_2(tri_led_driver_6_out_2), .out_3(tri_led_driver_6_out_3),
    .out_4(tri_led_driver_6_out_4));
  LED led_18 (.in(tri_led_driver_6_out_3));

  // Notes on the sheet:
  //   T0 -1, -1, -1 -- ok
  //   T1 -1, 0, -1 -- ok
  //   T2 -1, 1, -1 -- ok
  //   T3 0, 1, 0 -- BAD!
  //   Usually oscilates if you move it?!
  //   Initializes to unknown state, set both inputs to -1 to initialize
  //   *Almost* works.  Fails when one input moves two states, for example:
  //   If that's the case, B broke the rules here, and the C gate works
  //   Like the RS latch, we can set a rule, you must not advance until gate matches you.
endmodule
